// Logisim project morse.circ as structural Verilog: 4 circuits, main circuit main
module main (
);

  wire button_1_out, button_2_out, button_3_out, clock_1_out, clock_2_out, clock_3_out, clock_4_out,
       clock_5_out, keyboard_1_avail, morse_receiver_1_data_ready, morse_state_machine_1_data_ready,
       morse_transmitter_1_load_next_char, morse_transmitter_1_serial_out, or_1_out, rst;
  wire [3:0] morse_receiver_1_diagnostic_out, morse_state_machine_1_diagnostic_out, shift_register_1_out,
       shift_register_1_q0, shift_register_1_q1, shift_register_1_q2, shift_register_1_q3,
       shift_register_1_q4, shift_register_1_q5, shift_register_1_q6, shift_register_1_q7,
       shift_register_1_q8, shift_register_1_q9, shift_register_1_q10, shift_register_1_q11,
       shift_register_1_q12, shift_register_1_q13, shift_register_1_q14, shift_register_1_q15,
       shift_register_1_q16, shift_register_1_q17, shift_register_1_q18, shift_register_1_q19,
       shift_register_1_q20, shift_register_1_q21, shift_register_1_q22, shift_register_1_q23,
       shift_register_1_q24, shift_register_1_q25, shift_register_1_q26, shift_register_1_q27,
       shift_register_1_q28, shift_register_1_q29, shift_register_1_q30, shift_register_1_q31,
       shift_register_1_q32, shift_register_1_q33, shift_register_1_q34, shift_register_1_q35,
       shift_register_1_q36, shift_register_1_q37, shift_register_1_q38, shift_register_1_q39,
       shift_register_1_q40, shift_register_1_q41, shift_register_1_q42, shift_register_1_q43,
       shift_register_1_q44, shift_register_1_q45, shift_register_1_q46, shift_register_1_q47,
       shift_register_1_q48, shift_register_1_q49, shift_register_1_q50, shift_register_1_q51,
       shift_register_1_q52, shift_register_1_q53, shift_register_1_q54, shift_register_1_q55,
       shift_register_1_q56, shift_register_1_q57, shift_register_1_q58, shift_register_1_q59,
       shift_register_1_q60, shift_register_1_q61, shift_register_1_q62, shift_register_2_out,
       shift_register_2_q0, shift_register_2_q1, shift_register_2_q2, shift_register_2_q3,
       shift_register_2_q4, shift_register_2_q5, shift_register_2_q6, shift_register_2_q7,
       shift_register_2_q8, shift_register_2_q9, shift_register_2_q10, shift_register_2_q11,
       shift_register_2_q12, shift_register_2_q13, shift_register_2_q14, shift_register_2_q15,
       shift_register_2_q16, shift_register_2_q17, shift_register_2_q18, shift_register_2_q19,
       shift_register_2_q20, shift_register_2_q21, shift_register_2_q22, shift_register_2_q23,
       shift_register_2_q24, shift_register_2_q25, shift_register_2_q26, shift_register_2_q27,
       shift_register_2_q28, shift_register_2_q29, shift_register_2_q30, shift_register_2_q31,
       shift_register_2_q32, shift_register_2_q33, shift_register_2_q34, shift_register_2_q35,
       shift_register_2_q36, shift_register_2_q37, shift_register_2_q38, shift_register_2_q39,
       shift_register_2_q40, shift_register_2_q41, shift_register_2_q42, shift_register_2_q43,
       shift_register_2_q44, shift_register_2_q45, shift_register_2_q46, shift_register_2_q47,
       shift_register_2_q48, shift_register_2_q49, shift_register_2_q50, shift_register_2_q51,
       shift_register_2_q52, shift_register_2_q53, shift_register_2_q54, shift_register_2_q55,
       shift_register_2_q56, shift_register_2_q57, shift_register_2_q58, shift_register_2_q59,
       shift_register_2_q60, shift_register_2_q61, shift_register_2_q62;
  wire [6:0] keyboard_1_data;
  wire [7:0] morse_receiver_1_parallel_out, morse_state_machine_1_parallel_out;

  Keyboard keyboard_1 (
    .clk(morse_transmitter_1_load_next_char), .clr(or_1_out), .avail(keyboard_1_avail), .data(keyboard_1_data));  // open: re
  or or_1 (or_1_out, button_1_out, rst);
  Button button_1 (.out(button_1_out));
  POR por_1 (.out(rst));
  Clock clock_1 (.out(clock_1_out));
  Clock clock_2 (.out(clock_2_out));
  Shift_Register #(.length(64), .width(4)) shift_register_1 (
    .in(morse_receiver_1_diagnostic_out), .clk(clock_3_out), .out(shift_register_1_out),
    .q0(shift_register_1_q0), .q1(shift_register_1_q1), .q2(shift_register_1_q2), .q3(shift_register_1_q3),
    .q4(shift_register_1_q4), .q5(shift_register_1_q5), .q6(shift_register_1_q6), .q7(shift_register_1_q7),
    .q8(shift_register_1_q8), .q9(shift_register_1_q9), .q10(shift_register_1_q10),
    .q11(shift_register_1_q11), .q12(shift_register_1_q12), .q13(shift_register_1_q13),
    .q14(shift_register_1_q14), .q15(shift_register_1_q15), .q16(shift_register_1_q16),
    .q17(shift_register_1_q17), .q18(shift_register_1_q18), .q19(shift_register_1_q19),
    .q20(shift_register_1_q20), .q21(shift_register_1_q21), .q22(shift_register_1_q22),
    .q23(shift_register_1_q23), .q24(shift_register_1_q24), .q25(shift_register_1_q25),
    .q26(shift_register_1_q26), .q27(shift_register_1_q27), .q28(shift_register_1_q28),
    .q29(shift_register_1_q29), .q30(shift_register_1_q30), .q31(shift_register_1_q31),
    .q32(shift_register_1_q32), .q33(shift_register_1_q33), .q34(shift_register_1_q34),
    .q35(shift_register_1_q35), .q36(shift_register_1_q36), .q37(shift_register_1_q37),
    .q38(shift_register_1_q38), .q39(shift_register_1_q39), .q40(shift_register_1_q40),
    .q41(shift_register_1_q41), .q42(shift_register_1_q42), .q43(shift_register_1_q43),
    .q44(shift_register_1_q44), .q45(shift_register_1_q45), .q46(shift_register_1_q46),
    .q47(shift_register_1_q47), .q48(shift_register_1_q48), .q49(shift_register_1_q49),
    .q50(shift_register_1_q50), .q51(shift_register_1_q51), .q52(shift_register_1_q52),
    .q53(shift_register_1_q53), .q54(shift_register_1_q54), .q55(shift_register_1_q55),
    .q56(shift_register_1_q56), .q57(shift_register_1_q57), .q58(shift_register_1_q58),
    .q59(shift_register_1_q59), .q60(shift_register_1_q60), .q61(shift_register_1_q61),
    .q62(shift_register_1_q62), .q63(shift_register_1_out));  // open: shift, load, clr, d0, d1, d2, d3, d4, d5, d6, d7, d8, d9, d10, d11, d12, d13, d14, d15, d16, d17, d18, d19, d20, d21, d22, d23, d24, d25, d26, d27, d28, d29, d30, d31, d32, d33, d34, d35, d36, d37, d38, d39, d40, d41, d42, d43, d44, d45, d46, d47, d48, d49, d50, d51, d52, d53, d54, d55, d56, d57, d58, d59, d60, d61, d62, d63
  Clock clock_3 (.out(clock_3_out));
  DotMatrix #(.matrixcols(64), .matrixrows(4)) dotmatrix_1 (
    .col0(shift_register_1_q0), .col1(shift_register_1_q1), .col2(shift_register_1_q2),
    .col3(shift_register_1_q3), .col4(shift_register_1_q4), .col5(shift_register_1_q5),
    .col6(shift_register_1_q6), .col7(shift_register_1_q7), .col8(shift_register_1_q8),
    .col9(shift_register_1_q9), .col10(shift_register_1_q10), .col11(shift_register_1_q11),
    .col12(shift_register_1_q12), .col13(shift_register_1_q13), .col14(shift_register_1_q14),
    .col15(shift_register_1_q15), .col16(shift_register_1_q16), .col17(shift_register_1_q17),
    .col18(shift_register_1_q18), .col19(shift_register_1_q19), .col20(shift_register_1_q20),
    .col21(shift_register_1_q21), .col22(shift_register_1_q22), .col23(shift_register_1_q23),
    .col24(shift_register_1_q24), .col25(shift_register_1_q25), .col26(shift_register_1_q26),
    .col27(shift_register_1_q27), .col28(shift_register_1_q28), .col29(shift_register_1_q29),
    .col30(shift_register_1_q30), .col31(shift_register_1_q31), .col32(shift_register_1_q32),
    .col33(shift_register_1_q33), .col34(shift_register_1_q34), .col35(shift_register_1_q35),
    .col36(shift_register_1_q36), .col37(shift_register_1_q37), .col38(shift_register_1_q38),
    .col39(shift_register_1_q39), .col40(shift_register_1_q40), .col41(shift_register_1_q41),
    .col42(shift_register_1_q42), .col43(shift_register_1_q43), .col44(shift_register_1_q44),
    .col45(shift_register_1_q45), .col46(shift_register_1_q46), .col47(shift_register_1_q47),
    .col48(shift_register_1_q48), .col49(shift_register_1_q49), .col50(shift_register_1_q50),
    .col51(shift_register_1_q51), .col52(shift_register_1_q52), .col53(shift_register_1_q53),
    .col54(shift_register_1_q54), .col55(shift_register_1_q55), .col56(shift_register_1_q56),
    .col57(shift_register_1_q57), .col58(shift_register_1_q58), .col59(shift_register_1_q59),
    .col60(shift_register_1_q60), .col61(shift_register_1_q61), .col62(shift_register_1_q62),
    .col63(shift_register_1_out));
  morse_state_machine morse_state_machine_1 (
    .rst(rst), .clk(clock_2_out), .morse_in(morse_transmitter_1_serial_out),
    .parallel_out(morse_state_machine_1_parallel_out), .data_ready(morse_state_machine_1_data_ready),
    .diagnostic_out(morse_state_machine_1_diagnostic_out));
  Shift_Register #(.length(64), .width(4)) shift_register_2 (
    .in(morse_state_machine_1_diagnostic_out), .clk(clock_4_out), .out(shift_register_2_out),
    .q0(shift_register_2_q0), .q1(shift_register_2_q1), .q2(shift_register_2_q2), .q3(shift_register_2_q3),
    .q4(shift_register_2_q4), .q5(shift_register_2_q5), .q6(shift_register_2_q6), .q7(shift_register_2_q7),
    .q8(shift_register_2_q8), .q9(shift_register_2_q9), .q10(shift_register_2_q10),
    .q11(shift_register_2_q11), .q12(shift_register_2_q12), .q13(shift_register_2_q13),
    .q14(shift_register_2_q14), .q15(shift_register_2_q15), .q16(shift_register_2_q16),
    .q17(shift_register_2_q17), .q18(shift_register_2_q18), .q19(shift_register_2_q19),
    .q20(shift_register_2_q20), .q21(shift_register_2_q21), .q22(shift_register_2_q22),
    .q23(shift_register_2_q23), .q24(shift_register_2_q24), .q25(shift_register_2_q25),
    .q26(shift_register_2_q26), .q27(shift_register_2_q27), .q28(shift_register_2_q28),
    .q29(shift_register_2_q29), .q30(shift_register_2_q30), .q31(shift_register_2_q31),
    .q32(shift_register_2_q32), .q33(shift_register_2_q33), .q34(shift_register_2_q34),
    .q35(shift_register_2_q35), .q36(shift_register_2_q36), .q37(shift_register_2_q37),
    .q38(shift_register_2_q38), .q39(shift_register_2_q39), .q40(shift_register_2_q40),
    .q41(shift_register_2_q41), .q42(shift_register_2_q42), .q43(shift_register_2_q43),
    .q44(shift_register_2_q44), .q45(shift_register_2_q45), .q46(shift_register_2_q46),
    .q47(shift_register_2_q47), .q48(shift_register_2_q48), .q49(shift_register_2_q49),
    .q50(shift_register_2_q50), .q51(shift_register_2_q51), .q52(shift_register_2_q52),
    .q53(shift_register_2_q53), .q54(shift_register_2_q54), .q55(shift_register_2_q55),
    .q56(shift_register_2_q56), .q57(shift_register_2_q57), .q58(shift_register_2_q58),
    .q59(shift_register_2_q59), .q60(shift_register_2_q60), .q61(shift_register_2_q61),
    .q62(shift_register_2_q62), .q63(shift_register_2_out));  // open: shift, load, clr, d0, d1, d2, d3, d4, d5, d6, d7, d8, d9, d10, d11, d12, d13, d14, d15, d16, d17, d18, d19, d20, d21, d22, d23, d24, d25, d26, d27, d28, d29, d30, d31, d32, d33, d34, d35, d36, d37, d38, d39, d40, d41, d42, d43, d44, d45, d46, d47, d48, d49, d50, d51, d52, d53, d54, d55, d56, d57, d58, d59, d60, d61, d62, d63
  Clock clock_4 (.out(clock_4_out));
  DotMatrix #(.matrixcols(64), .matrixrows(4)) dotmatrix_2 (
    .col0(shift_register_2_q0), .col1(shift_register_2_q1), .col2(shift_register_2_q2),
    .col3(shift_register_2_q3), .col4(shift_register_2_q4), .col5(shift_register_2_q5),
    .col6(shift_register_2_q6), .col7(shift_register_2_q7), .col8(shift_register_2_q8),
    .col9(shift_register_2_q9), .col10(shift_register_2_q10), .col11(shift_register_2_q11),
    .col12(shift_register_2_q12), .col13(shift_register_2_q13), .col14(shift_register_2_q14),
    .col15(shift_register_2_q15), .col16(shift_register_2_q16), .col17(shift_register_2_q17),
    .col18(shift_register_2_q18), .col19(shift_register_2_q19), .col20(shift_register_2_q20),
    .col21(shift_register_2_q21), .col22(shift_register_2_q22), .col23(shift_register_2_q23),
    .col24(shift_register_2_q24), .col25(shift_register_2_q25), .col26(shift_register_2_q26),
    .col27(shift_register_2_q27), .col28(shift_register_2_q28), .col29(shift_register_2_q29),
    .col30(shift_register_2_q30), .col31(shift_register_2_q31), .col32(shift_register_2_q32),
    .col33(shift_register_2_q33), .col34(shift_register_2_q34), .col35(shift_register_2_q35),
    .col36(shift_register_2_q36), .col37(shift_register_2_q37), .col38(shift_register_2_q38),
    .col39(shift_register_2_q39), .col40(shift_register_2_q40), .col41(shift_register_2_q41),
    .col42(shift_register_2_q42), .col43(shift_register_2_q43), .col44(shift_register_2_q44),
    .col45(shift_register_2_q45), .col46(shift_register_2_q46), .col47(shift_register_2_q47),
    .col48(shift_register_2_q48), .col49(shift_register_2_q49), .col50(shift_register_2_q50),
    .col51(shift_register_2_q51), .col52(shift_register_2_q52), .col53(shift_register_2_q53),
    .col54(shift_register_2_q54), .col55(shift_register_2_q55), .col56(shift_register_2_q56),
    .col57(shift_register_2_q57), .col58(shift_register_2_q58), .col59(shift_register_2_q59),
    .col60(shift_register_2_q60), .col61(shift_register_2_q61), .col62(shift_register_2_q62),
    .col63(shift_register_2_out));
  morse_transmitter morse_transmitter_1 (
    .clk(clock_1_out), .char_available(keyboard_1_avail), .parallel_in({1'b0, keyboard_1_data}), .rst(rst),
    .load_next_char(morse_transmitter_1_load_next_char), .serial_out(morse_transmitter_1_serial_out));
  LED led_1 (.in(morse_transmitter_1_serial_out));
  Clock clock_5 (.out(clock_5_out));
  // Probe on morse_state_machine_1_parallel_out
  // Probe on morse_state_machine_1_parallel_out[6:0]
  TTY tty_1 (
    .data(morse_state_machine_1_parallel_out[6:0]), .clk(morse_state_machine_1_data_ready), .clr(button_2_out));  // open: we
  Button button_2 (.out(button_2_out));
  // Probe on morse_receiver_1_parallel_out[6:0]
  morse_receiver morse_receiver_1 (
    .rst(rst), .clk(clock_5_out), .morse_in(morse_transmitter_1_serial_out),
    .parallel_out(morse_receiver_1_parallel_out), .data_ready(morse_receiver_1_data_ready),
    .diagnostic_out(morse_receiver_1_diagnostic_out));
  TTY tty_2 (
    .data(morse_receiver_1_parallel_out[6:0]), .clk(morse_receiver_1_data_ready), .clr(button_3_out));  // open: we
  Button button_3 (.out(button_3_out));
endmodule

module morse_transmitter (
  input  clk,
  input  char_available,
  input  [7:0] parallel_in,
  input  rst,
  output load_next_char,
  output serial_out
);

  wire and_1_out, bit_ready, buffer_1_out, buffer_2_out, buffer_3_out, buffer_4_out, buffer_5_out,
       buffer_6_out, buffer_7_out, buffer_8_out, buffer_10_out, buffer_11_out, buffer_12_out, buffer_13_out,
       buffer_14_out, buffer_15_out, buffer_16_out, buffer_17_out, buffer_18_out, buffer_19_out,
       buffer_20_out, buffer_21_out, buffer_22_out, buffer_23_out, buffer_24_out, buffer_25_out,
       counter_1_carry, counter_2_carry, counter_3_carry, counter_4_carry, counter_5_carry, dash, dot,
       not_1_out, not_2_out, or_1_out, shift_bits, shift_register_1_q0, shift_register_1_q1,
       shift_register_1_q2, shift_register_1_q3, shift_register_1_q4, shift_register_1_q5,
       shift_register_1_q6, shifter_empty, shifter_not_empty, space, transmitter_idle;
  wire [0:0] shift_register_1_out;
  wire [7:0] Morse_Codes_data;

  ROM Morse_Codes (.addr(parallel_in), .data(Morse_Codes_data));
  buf buffer_1 (buffer_1_out, shifter_empty);
  buf buffer_2 (buffer_2_out, buffer_5_out);
  buf buffer_3 (buffer_3_out, buffer_2_out);
  buf buffer_4 (buffer_4_out, buffer_3_out);
  buf buffer_5 (buffer_5_out, buffer_1_out);
  or or_1 (or_1_out, shift_bits, load_next_char);
  buf buffer_6 (buffer_6_out, buffer_7_out);
  buf buffer_7 (buffer_7_out, buffer_17_out);
  buf buffer_8 (buffer_8_out, buffer_6_out);
  buf buffer_9 (bit_ready, buffer_8_out);
  buf buffer_10 (buffer_10_out, buffer_4_out);
  buf buffer_11 (buffer_11_out, buffer_10_out);
  buf buffer_12 (buffer_12_out, buffer_11_out);
  buf buffer_13 (buffer_13_out, buffer_12_out);
  buf buffer_14 (buffer_14_out, char_available);
  buf buffer_15 (buffer_15_out, buffer_14_out);
  buf buffer_16 (buffer_16_out, buffer_15_out);
  not not_1 (not_1_out, or_1_out);
  and and_1 (and_1_out, not_1_out, or_1_out);
  buf buffer_17 (buffer_17_out, buffer_18_out);
  buf buffer_18 (buffer_18_out, and_1_out);
  buf buffer_19 (buffer_19_out, buffer_13_out);
  buf buffer_20 (buffer_20_out, buffer_19_out);
  buf buffer_21 (buffer_21_out, buffer_20_out);
  buf buffer_22 (buffer_22_out, buffer_21_out);
  buf buffer_23 (buffer_23_out, buffer_16_out);
  buf buffer_24 (buffer_24_out, buffer_23_out);
  buf buffer_25 (buffer_25_out, buffer_24_out);
  and and_2 (shift_bits, shifter_not_empty, transmitter_idle);
  // Probe on Morse_Codes_data
  not not_2 (not_2_out, shifter_not_empty);
  Shift_Register shift_register_1 (
    .shift(shifter_not_empty), .in(1'b0), .clk(and_1_out), .out(shift_register_1_out[0]), .load(not_2_out),
    .clr(rst), .d0(Morse_Codes_data[7]), .q0(shift_register_1_q0), .d1(Morse_Codes_data[6]),
    .q1(shift_register_1_q1), .d2(Morse_Codes_data[5]), .q2(shift_register_1_q2), .d3(Morse_Codes_data[4]),
    .q3(shift_register_1_q3), .d4(Morse_Codes_data[3]), .q4(shift_register_1_q4), .d5(Morse_Codes_data[2]),
    .q5(shift_register_1_q5), .d6(Morse_Codes_data[1]), .q6(shift_register_1_q6), .d7(Morse_Codes_data[0]));  // open: q7
  not not_3 (shifter_empty, shifter_not_empty);
  and and_3 (load_next_char, buffer_22_out, buffer_25_out, transmitter_idle);
  or or_2 (shifter_not_empty, shift_register_1_q0, shift_register_1_q1, shift_register_1_q2, shift_register_1_q3, shift_register_1_q4, shift_register_1_q5, shift_register_1_q6);
  Demultiplexer #(.enable("false"), .select(2)) demultiplexer_1 (
    .out1(space), .out2(dot), .out3(dash), .in(bit_ready), .sel({shifter_not_empty, shift_register_1_out[0]}));  // open: out0
  Counter #(.max('h3), .ongoal("stay")) counter_1 (
    .load(rst), .D(8'h3), .carry(counter_1_carry), .clk(clk), .clr(dot));  // open: count, Q, up
  Counter #(.max('h9), .ongoal("stay")) counter_2 (
    .load(rst), .D(8'h9), .carry(counter_2_carry), .clk(clk), .clr(dash));  // open: count, Q, up
  Counter #(.max('h9), .ongoal("stay")) counter_3 (
    .load(rst), .D(8'h9), .carry(counter_3_carry), .clk(clk), .clr(space));  // open: count, Q, up
  Counter #(.max('h3), .ongoal("stay")) counter_4 (
    .load(rst), .D(8'h3), .count(counter_1_carry), .carry(counter_4_carry), .clk(clk), .clr(dot));  // open: Q, up
  Counter #(.max('h3), .ongoal("stay")) counter_5 (
    .load(rst), .D(8'h3), .count(counter_2_carry), .carry(counter_5_carry), .clk(clk), .clr(dash));  // open: Q, up
  or or_3 (serial_out, ~counter_1_carry, ~counter_2_carry);  // OR_Gate
  and and_4 (transmitter_idle, counter_4_carry, counter_5_carry, counter_3_carry);

  // Notes on the sheet:
  //   contents of Morse_Codes (hex, n*v repeats v):
  //   32*0 1 67 52 0 0 0 22 5e 2d 6d 0 2a 73 61 6a 29 3f 3e 3c 38 30 20 21 23 27 2f 47 35 0 31 0 4c 56 6
  //   11 15 9 2 14 b 10 4 1e d 12 7 5 f 16 1b a 8 3 c 18 e 19 1d 13 0 39 0 0 6c 0 6 11 15 9 2 14 b 10 4 1e
  //   d 12 7 5 f 16 1b a 8 3 c 18 e 19 1d 13 69*0 36 0 0 0 1a 0 0 0 32 24 6*0 2c 5*0 17 5*0 1c 0 0 0 36 0
  //   0 0 1a 0 0 0 32 24 6*0 2c 5*0 17 5*0 1c
endmodule

module morse_receiver (
  input  rst,
  input  clk,
  input  morse_in,
  output [7:0] parallel_out,
  output data_ready,
  output [3:0] diagnostic_out
);

  wire and_1_out, and_2_out, buffer_1_out, buffer_2_out, buffer_3_out, buffer_4_out, buffer_5_out,
       buffer_6_out, buffer_7_out, buffer_8_out, buffer_9_out, buffer_10_out, buffer_11_out, buffer_12_out,
       buffer_13_out, buffer_14_out, buffer_15_out, buffer_16_out, buffer_17_out, buffer_18_out,
       buffer_19_out, buffer_20_out, buffer_21_out, buffer_22_out, buffer_23_out, buffer_24_out,
       buffer_25_out, buffer_26_out, buffer_27_out, buffer_28_out, nor_1_out, nor_2_out, not_1_out,
       not_2_out, not_3_out, not_4_out, not_5_out, not_6_out, or_1_out, shift_register_1_out;
  wire [6:0] shift_register_1_q0;

  Counter #(.max('h6), .ongoal("stay"), .width(3)) counter_1 (
    .load(rst), .D(3'b110), .carry(diagnostic_out[1]), .clk(clk), .clr(morse_in));  // open: count, Q, up
  Counter #(.max('h8), .ongoal("stay"), .width(4)) counter_2 (
    .load(rst), .D(4'b1000), .count(diagnostic_out[1]), .carry(diagnostic_out[0]), .clk(clk), .clr(morse_in));  // open: Q, up
  Counter #(.max('h5), .ongoal("stay"), .width(3)) counter_3 (
    .carry(diagnostic_out[2]), .clk(clk), .clr(not_1_out));  // open: load, D, count, Q, up
  not not_1 (not_1_out, morse_in);
  not not_2 (not_2_out, diagnostic_out[0]);
  not not_3 (not_3_out, diagnostic_out[1]);
  buf buffer_1 (buffer_1_out, diagnostic_out[2]);
  buf buffer_2 (buffer_2_out, buffer_1_out);
  buf buffer_3 (buffer_3_out, buffer_2_out);
  not not_4 (not_4_out, diagnostic_out[1]);
  buf buffer_4 (buffer_4_out, diagnostic_out[1]);
  buf buffer_5 (buffer_5_out, buffer_4_out);
  and and_1 (and_1_out, not_2_out, diagnostic_out[0]);
  buf buffer_6 (buffer_6_out, and_1_out);
  and and_2 (and_2_out, not_3_out, diagnostic_out[1]);
  buf buffer_7 (buffer_7_out, buffer_3_out);
  buf buffer_8 (buffer_8_out, buffer_7_out);
  buf buffer_9 (buffer_9_out, buffer_8_out);
  nor nor_1 (nor_1_out, morse_in, not_5_out);
  not not_5 (not_5_out, morse_in);
  nor nor_2 (nor_2_out, not_4_out, diagnostic_out[1]);
  buf buffer_10 (buffer_10_out, buffer_5_out);
  buf buffer_11 (buffer_11_out, buffer_10_out);
  buf buffer_12 (buffer_12_out, buffer_11_out);
  buf buffer_13 (buffer_13_out, buffer_6_out);
  buf buffer_14 (buffer_14_out, buffer_13_out);
  buf buffer_15 (buffer_15_out, buffer_14_out);
  buf buffer_16 (buffer_16_out, buffer_15_out);
  or or_1 (or_1_out, nor_1_out, nor_2_out, and_1_out);
  buf buffer_17 (buffer_17_out, buffer_12_out);
  buf buffer_18 (buffer_18_out, buffer_16_out);
  buf buffer_19 (buffer_19_out, buffer_18_out);
  buf buffer_20 (buffer_20_out, buffer_19_out);
  buf buffer_21 (buffer_21_out, buffer_20_out);
  not not_6 (not_6_out, buffer_17_out);
  Shift_Register shift_register_1 (
    .shift(not_6_out), .in(buffer_9_out), .clk(or_1_out), .out(shift_register_1_out), .load(buffer_17_out),
    .clr(rst), .d0(1'b1), .q0(shift_register_1_q0[0]), .d1(1'b0), .q1(shift_register_1_q0[1]), .d2(1'b0),
    .q2(shift_register_1_q0[2]), .d3(1'b0), .q3(shift_register_1_q0[3]), .d4(1'b0),
    .q4(shift_register_1_q0[4]), .d5(1'b0), .q5(shift_register_1_q0[5]), .d6(1'b0),
    .q6(shift_register_1_q0[6]), .d7(1'b0), .q7(shift_register_1_out));
  buf buffer_22 (buffer_22_out, buffer_21_out);
  buf buffer_23 (buffer_23_out, buffer_22_out);
  buf buffer_24 (buffer_24_out, buffer_23_out);
  buf buffer_25 (buffer_25_out, buffer_24_out);
  ROM #(.addrWidth(7)) rom_1 (.addr(shift_register_1_q0), .data(parallel_out));
  buf buffer_26 (buffer_26_out, buffer_25_out);
  buf buffer_27 (buffer_27_out, buffer_26_out);
  buf buffer_28 (buffer_28_out, buffer_27_out);
  or or_2 (data_ready, buffer_28_out, and_2_out);

  assign diagnostic_out[3] = morse_in;

  // Notes on the sheet:
  //   contents of rom_1 (hex, n*v repeats v):
  //   0 20 65 74 69 61 6e 6d 73 75 72 77 64 6b 67 6f 68 76 66 fc 6c e4 70 6a 62 78 63 79 7a 71 f6 20 35 34
  //   0 33 e9 0 f0 32 26 e8 2b 0 0 e0 0 31 36 3d 2f 5c 0 3b 28 0 37 20 0 0 38 0 39 30 12*0 3f 5f 4*0 22 0
  //   0 2e 4*0 40 0 0 0 27 0 0 2d 11*0 29 5*0 2c 4*0 3a 21 d1 a8 9d d2 25 31
endmodule

module morse_state_machine (
  input  rst,
  input  clk,
  input  morse_in,
  output [7:0] parallel_out,
  output data_ready,
  output [3:0] diagnostic_out
);

  wire and_1_out, and_2_out, buffer_1_out, buffer_2_out, buffer_3_out, buffer_4_out, buffer_5_out,
       buffer_7_out, buffer_8_out, buffer_9_out, buffer_10_out, buffer_11_out, buffer_13_out, buffer_14_out,
       buffer_15_out, buffer_16_out, counter_1_carry, not_1_out, not_2_out, not_3_out, reset_state;
  wire [6:0] multiplexer_1_out;
  wire [7:0] morse_statemachine_data;

  // Probe on {reset_state, diagnostic_out[1], morse_in, multiplexer_1_out}
  buf buffer_1 (buffer_1_out, diagnostic_out[2]);
  buf buffer_2 (buffer_2_out, buffer_1_out);
  buf buffer_3 (buffer_3_out, buffer_2_out);
  buf buffer_4 (buffer_4_out, buffer_3_out);
  ROM #(.addrWidth(10)) morse_statemachine (
    .addr({reset_state, diagnostic_out[1], morse_in, multiplexer_1_out}), .data(morse_statemachine_data));
  Multiplexer #(.enable("false"), .width(7)) multiplexer_1 (
    .in0(morse_statemachine_data[6:0]), .in1({7{1'b0}}), .out(multiplexer_1_out), .sel(rst));
  Counter #(.max('h5), .ongoal("stay"), .width(3)) counter_1 (
    .carry(counter_1_carry), .clk(clk), .clr(not_1_out));  // open: load, D, count, Q, up
  not not_1 (not_1_out, morse_in);
  buf buffer_5 (buffer_5_out, buffer_4_out);
  buf buffer_6 (reset_state, buffer_5_out);
  buf buffer_7 (buffer_7_out, counter_1_carry);
  buf buffer_8 (buffer_8_out, buffer_7_out);
  buf buffer_9 (buffer_9_out, buffer_8_out);
  buf buffer_10 (buffer_10_out, buffer_9_out);
  // Probe on morse_statemachine_data[6:0]
  buf buffer_11 (buffer_11_out, buffer_10_out);
  buf buffer_12 (diagnostic_out[1], buffer_11_out);
  // Probe on morse_statemachine_data[5:0]
  ROM #(.addrWidth(7)) hypercube2chr2bin (.addr({1'b0, morse_statemachine_data[5:0]}), .data(parallel_out));
  Counter #(.max('h6), .ongoal("stay"), .width(3)) counter_2 (
    .load(rst), .D(3'b110), .carry(diagnostic_out[2]), .clk(clk), .clr(morse_in));  // open: count, Q, up
  not not_2 (not_2_out, diagnostic_out[3]);
  buf buffer_13 (buffer_13_out, not_2_out);
  buf buffer_14 (buffer_14_out, buffer_13_out);
  and and_1 (and_1_out, buffer_14_out, diagnostic_out[3]);
  not not_3 (not_3_out, diagnostic_out[2]);
  buf buffer_15 (buffer_15_out, not_3_out);
  buf buffer_16 (buffer_16_out, buffer_15_out);
  and and_2 (and_2_out, buffer_16_out, diagnostic_out[2]);
  or or_1 (data_ready, and_1_out, and_2_out);
  Counter #(.max('hd), .ongoal("stay"), .width(4)) counter_3 (
    .load(rst), .D(4'b1101), .carry(diagnostic_out[3]), .clk(clk), .clr(morse_in));  // open: count, Q, up

  assign diagnostic_out[0] = morse_in;

  // Other names for the same wires on the sheet: morse = morse_in; data = diagnostic_out[1];
  //   char_received = diagnostic_out[2]; word_received = diagnostic_out[3]

  // Notes on the sheet:
  //   contents of morse_statemachine (hex, n*v repeats v):
  //   0 a1 83 83 c4 85 86 a7 98 89 8a 8f 8c ad ce 8f 92 91 92 d3 94 91 d6 97 98 d9 da 9b 9d 9d 9e df b0 a1
  //   a2 e3 a4 85 e6 a7 a8 e9 ae ab ec ad ae ef b0 f1 ba b3 f4 b5 b6 f7 f8 b9 ba fb bc b9 bf bf c1 c1 c2
  //   cb c4 c4 86 c7 c8 c8 8a cb 8c cd ce df d0 91 92 d3 94 d5 d6 d6 d9 d9 da da dc 9d 9e df e0 e0 ea e3
  //   a4 e5 e6 a7 e9 e9 ea ab ec ad ef ef f1 f1 f2 f7 f4 d5 b6 f7 f8 b9 fe fb bc fd fe bf c0 81 82 c3 84
  //   c5 c6 87 88 c9 ca 8b cc 8d 8e cf 90 d1 d2 93 d4 95 96 d7 d8 99 9a db 9c dd de 9f a0 e1 e2 a3 e4 a5
  //   a6 e7 e8 a9 aa eb ac ed ee af f0 b1 b2 f3 b4 f5 f6 b7 b8 f9 fa bb fc bd be ff c0 81 82 c3 84 c5 c6
  //   87 88 c9 ca 8b cc 8d 8e cf 90 d1 d2 93 d4 95 96 d7 d8 99 9a db 9c dd de 9f a0 e1 e2 a3 e4 a5 a6 e7
  //   e8 a9 aa eb ac ed ee af f0 b1 b2 f3 b4 f5 f6 b7 b8 f9 fa bb fc bd be ff 0 89 a2 83 c4 85 86 97 a8 89
  //   8a 9b 8c 8c ce 8f d0 91 92 d3 94 94 86 97 98 d9 da 9b dc 9d 9e 9e a4 a1 a2 e3 a4 b5 e6 a7 a8 ab 8a
  //   ab bc ad ae ef b0 f1 b3 b3 f4 b5 b6 f7 f8 b9 ba fb bc fd b6 bf c2 c1 c2 c7 c4 85 86 c7 c8 cd 8a cb
  //   dc cd ce ce d0 91 92 d3 94 d5 d6 97 d0 d9 da d3 dc 9d 9e df e0 e5 f2 e3 e6 e5 e6 e3 a8 e9 ea ab ec
  //   fd ec ef f8 f1 f2 fb f4 f4 b6 f7 f8 b9 ba fb bc fd fe bf c0 81 82 c3 84 c5 c6 87 88 c9 ca 8b cc 8d
  //   8e cf 90 d1 d2 93 d4 95 96 d7 d8 99 9a db 9c dd de 9f a0 e1 e2 a3 e4 a5 a6 e7 e8 a9 aa eb ac ed ee
  //   af f0 b1 b2 f3 b4 f5 f6 b7 b8 f9 fa bb fc bd be ff c0 81 82 c3 84 c5 c6 87 88 c9 ca 8b cc 8d 8e cf
  //   90 d1 d2 93 d4 95 96 d7 d8 99 9a db 9c dd de 9f a0 e1 e2 a3 e4 a5 a6 e7 e8 a9 aa eb ac ed ee af f0
  //   b1 b2 f3 b4 f5 f6 b7 b8 f9 fa bb fc bd be ff 0 0 0 82 85 a5 96 83 89 81 aa 83 8d 89 8f 8b 98 95 90
  //   9b 95 b5 97 87 88 98 9b 8b 8c 9c 9f 8f a1 81 82 a7 a0 a1 a4 87 88 a8 a2 a9 ae 8d aa ae a0 b0 a2 b2
  //   b5 a5 be b3 b0 bd b2 b3 ac ad ba be 0 1 2 3 4 5 6 7 8 9 a b c d e f 10 11 12 13 14 15 16 17 18 19 1a
  //   1b 1c 1d 1e 1f 20 21 22 23 24 25 26 27 28 29 2a 2b 2c 2d 2e 2f 30 31 32 33 34 35 36 37 38 39 3a 3b
  //   3c 3d 3e 3f 80 80 80 82 85 a5 96 83 89 81 aa 83 8d 89 8f 8b 98 95 90 9b 95 b5 97 87 88 98 9b 8b 8c
  //   9c 9f 8f a1 81 82 a7 a0 a1 a4 87 88 a8 a2 a9 ae 8d aa ae a0 b0 a2 b2 b5 a5 be b3 b0 bd b2 b3 ac ad
  //   ba be 0 1 2 3 4 5 6 7 8 9 a b c d e f 10 11 12 13 14 15 16 17 18 19 1a 1b 1c 1d 1e 1f 20 21 22 23 24
  //   25 26 27 28 29 2a 2b 2c 2d 2e 2f 30 31 32 33 34 35 36 37 38 39 3a 3b 3c 3d 3e 3f 80 80 80 82 85 a5
  //   96 83 89 81 aa 83 8d 89 8f 8b 98 95 90 9b 95 b5 97 87 88 98 9b 8b 8c 9c 9f 8f a1 81 82 a7 a0 a1 a4
  //   87 88 a8 a2 a9 ae 8d aa ae a0 b0 a2 b2 b5 a5 be b3 b0 bd b2 b3 ac ad ba be 0 1 2 3 4 5 6 7 8 9 a b c
  //   d e f 10 11 12 13 14 15 16 17 18 19 1a 1b 1c 1d 1e 1f 20 21 22 23 24 25 26 27 28 29 2a 2b 2c 2d 2e
  //   2f 30 31 32 33 34 35 36 37 38 39 3a 3b 3c 3d 3e 3f 80 80 80 82 85 a5 96 83 89 81 aa 83 8d 89 8f 8b
  //   98 95 90 9b 95 b5 97 87 88 98 9b 8b 8c 9c 9f 8f a1 81 82 a7 a0 a1 a4 87 88 a8 a2 a9 ae 8d aa ae a0
  //   b0 a2 b2 b5 a5 be b3 b0 bd b2 b3 ac ad ba be 0 1 2 3 4 5 6 7 8 9 a b c d e f 10 11 12 13 14 15 16 17
  //   18 19 1a 1b 1c 1d 1e 1f 20 21 22 23 24 25 26 27 28 29 2a 2b 2c 2d 2e 2f 30 31 32 33 34 35 36 37 38
  //   39 3a 3b 3c 3d 3e 3f
  //   contents of hypercube2chr2bin (hex, n*v repeats v):
  //   20 65 74 6e e9 66 29 6b 72 61 71 64 6a 77 3d 62 e8 3f 22 5c 5f f0 28 79 6c 26 2f 78 31 27 2d 36 73
  //   69 6d 3b 76 75 33 63 e4 2b 67 2e 20 70 7a 37 68 35 6f 20 32 fc 21 39 34 40 f6 30 2c e0 38 3a 1 2 3 6
  //   24 12 6d d a 5 1d c 17 b 31 18 29 4c 52 33 4d 26 36 1b 14 28 32 19 2f 5e 61 30 8 4 7 35 11 9 23 1a
  //   15 2a e 55 39 16 1c 38 10 20 f 1f 27 13 79 3e 21 5a 1e 3f 73 2d 3c 78
endmodule
