// Logisim project morse2serial.circ as structural Verilog: 7 circuits, main circuit main
module main (
);

  wire buffer_1_out, buffer_2_out, buffer_3_out, buffer_4_out, buffer_5_out, button_1_out, button_2_out,
       char_received, clk1, clk2, clk4, clk8, counter_2_carry, data,
       eprom_morse_transmitter_1_load_next_char, eprom_uart_receiver_1_data_ready,
       eprom_uart_receiver_1_framing_error, eprom_uart_receiver_1_parity_error, keyboard_1_avail, morse,
       not_1_out, not_2_out, or_1_out, or_3_out, por_1_out, reset_state, rst, rst_out, serial, t_ff_1_q,
       t_ff_2_q, word_received;
  wire [5:0] multiplexer_1_out;
  wire [5:5] t_ff_3_q;
  wire [6:0] keyboard_1_data, pull_resistor_1_node, shift_register_1_out, shift_register_1_q0,
       shift_register_1_q1, shift_register_1_q2, shift_register_1_q3, shift_register_1_q4,
       shift_register_1_q5, shift_register_1_q6, shift_register_1_q7, shift_register_1_q8,
       shift_register_1_q9, shift_register_1_q10, shift_register_1_q11, shift_register_1_q12,
       shift_register_1_q13, shift_register_1_q14, shift_register_1_q15, shift_register_1_q16,
       shift_register_1_q17, shift_register_1_q18, shift_register_1_q19, shift_register_1_q20,
       shift_register_1_q21, shift_register_1_q22, shift_register_1_q23, shift_register_1_q24,
       shift_register_1_q25, shift_register_1_q26, shift_register_1_q27, shift_register_1_q28,
       shift_register_1_q29, shift_register_1_q30, shift_register_1_q31, shift_register_1_q32,
       shift_register_1_q33, shift_register_1_q34, shift_register_1_q35, shift_register_1_q36,
       shift_register_1_q37, shift_register_1_q38, shift_register_1_q39, shift_register_1_q40,
       shift_register_1_q41, shift_register_1_q42, shift_register_1_q43, shift_register_1_q44,
       shift_register_1_q45, shift_register_1_q46, shift_register_1_q47, shift_register_1_q48,
       shift_register_1_q49, shift_register_1_q50, shift_register_1_q51, shift_register_1_q52,
       shift_register_1_q53, shift_register_1_q54, shift_register_1_q55, shift_register_1_q56,
       shift_register_1_q57, shift_register_1_q58, shift_register_1_q59, shift_register_1_q60,
       shift_register_1_q61, shift_register_1_q62;
  wire [7:0] eprom_uart_receiver_1_data_out, MORSE_RECEIVER_ROM_data, SERIAL_TRANSMITTER_ROM_data;
  wire [7:7] pull_resistor_1_node_2;
  wire [8:4] counter_1_q;

  Keyboard keyboard_1 (
    .clk(eprom_morse_transmitter_1_load_next_char), .clr(or_1_out), .avail(keyboard_1_avail),
    .data(keyboard_1_data));  // open: re
  or or_1 (or_1_out, button_1_out, rst);
  Button button_1 (.out(button_1_out));
  Counter counter_1 (.Q({counter_1_q, clk8, clk4, clk2}), .clk(clk1));  // open: load, D, count, carry, up, clr
  Clock clock_1 (.out(clk1));
  Counter #(.max('h5), .ongoal("stay"), .width(3)) counter_2 (
    .carry(counter_2_carry), .clk(clk8), .clr(not_1_out));  // open: load, D, count, Q, up
  not not_1 (not_1_out, morse);
  ROM #(.addrWidth(15)) MORSE_RECEIVER_ROM (
    .addr({5'b01000, reset_state, data, morse, pull_resistor_1_node}), .data(MORSE_RECEIVER_ROM_data));
  // Probe on pull_resistor_1_node
  POR por_1 (.out(por_1_out));
  Button u_rst (.out(rst_out));
  buf buffer_1 (buffer_1_out, counter_2_carry);
  buf buffer_2 (buffer_2_out, buffer_1_out);
  buf buffer_3 (buffer_3_out, buffer_2_out);
  buf buffer_4 (buffer_4_out, buffer_3_out);
  // Probe on {reset_state, data, morse, pull_resistor_1_node}
  Shift_Register #(.length(64), .width(7)) shift_register_1 (
    .in({morse, data, char_received, word_received, serial, reset_state, clk4}), .clk(clk2),
    .out(shift_register_1_out), .q0(shift_register_1_q0), .q1(shift_register_1_q1), .q2(shift_register_1_q2),
    .q3(shift_register_1_q3), .q4(shift_register_1_q4), .q5(shift_register_1_q5), .q6(shift_register_1_q6),
    .q7(shift_register_1_q7), .q8(shift_register_1_q8), .q9(shift_register_1_q9), .q10(shift_register_1_q10),
    .q11(shift_register_1_q11), .q12(shift_register_1_q12), .q13(shift_register_1_q13),
    .q14(shift_register_1_q14), .q15(shift_register_1_q15), .q16(shift_register_1_q16),
    .q17(shift_register_1_q17), .q18(shift_register_1_q18), .q19(shift_register_1_q19),
    .q20(shift_register_1_q20), .q21(shift_register_1_q21), .q22(shift_register_1_q22),
    .q23(shift_register_1_q23), .q24(shift_register_1_q24), .q25(shift_register_1_q25),
    .q26(shift_register_1_q26), .q27(shift_register_1_q27), .q28(shift_register_1_q28),
    .q29(shift_register_1_q29), .q30(shift_register_1_q30), .q31(shift_register_1_q31),
    .q32(shift_register_1_q32), .q33(shift_register_1_q33), .q34(shift_register_1_q34),
    .q35(shift_register_1_q35), .q36(shift_register_1_q36), .q37(shift_register_1_q37),
    .q38(shift_register_1_q38), .q39(shift_register_1_q39), .q40(shift_register_1_q40),
    .q41(shift_register_1_q41), .q42(shift_register_1_q42), .q43(shift_register_1_q43),
    .q44(shift_register_1_q44), .q45(shift_register_1_q45), .q46(shift_register_1_q46),
    .q47(shift_register_1_q47), .q48(shift_register_1_q48), .q49(shift_register_1_q49),
    .q50(shift_register_1_q50), .q51(shift_register_1_q51), .q52(shift_register_1_q52),
    .q53(shift_register_1_q53), .q54(shift_register_1_q54), .q55(shift_register_1_q55),
    .q56(shift_register_1_q56), .q57(shift_register_1_q57), .q58(shift_register_1_q58),
    .q59(shift_register_1_q59), .q60(shift_register_1_q60), .q61(shift_register_1_q61),
    .q62(shift_register_1_q62), .q63(shift_register_1_out));  // open: shift, load, clr, d0, d1, d2, d3, d4, d5, d6, d7, d8, d9, d10, d11, d12, d13, d14, d15, d16, d17, d18, d19, d20, d21, d22, d23, d24, d25, d26, d27, d28, d29, d30, d31, d32, d33, d34, d35, d36, d37, d38, d39, d40, d41, d42, d43, d44, d45, d46, d47, d48, d49, d50, d51, d52, d53, d54, d55, d56, d57, d58, d59, d60, d61, d62, d63
  DotMatrix #(.matrixcols(64)) dotmatrix_1 (
    .col0(shift_register_1_q0), .col1(shift_register_1_q1), .col2(shift_register_1_q2),
    .col3(shift_register_1_q3), .col4(shift_register_1_q4), .col5(shift_register_1_q5),
    .col6(shift_register_1_q6), .col7(shift_register_1_q7), .col8(shift_register_1_q8),
    .col9(shift_register_1_q9), .col10(shift_register_1_q10), .col11(shift_register_1_q11),
    .col12(shift_register_1_q12), .col13(shift_register_1_q13), .col14(shift_register_1_q14),
    .col15(shift_register_1_q15), .col16(shift_register_1_q16), .col17(shift_register_1_q17),
    .col18(shift_register_1_q18), .col19(shift_register_1_q19), .col20(shift_register_1_q20),
    .col21(shift_register_1_q21), .col22(shift_register_1_q22), .col23(shift_register_1_q23),
    .col24(shift_register_1_q24), .col25(shift_register_1_q25), .col26(shift_register_1_q26),
    .col27(shift_register_1_q27), .col28(shift_register_1_q28), .col29(shift_register_1_q29),
    .col30(shift_register_1_q30), .col31(shift_register_1_q31), .col32(shift_register_1_q32),
    .col33(shift_register_1_q33), .col34(shift_register_1_q34), .col35(shift_register_1_q35),
    .col36(shift_register_1_q36), .col37(shift_register_1_q37), .col38(shift_register_1_q38),
    .col39(shift_register_1_q39), .col40(shift_register_1_q40), .col41(shift_register_1_q41),
    .col42(shift_register_1_q42), .col43(shift_register_1_q43), .col44(shift_register_1_q44),
    .col45(shift_register_1_q45), .col46(shift_register_1_q46), .col47(shift_register_1_q47),
    .col48(shift_register_1_q48), .col49(shift_register_1_q49), .col50(shift_register_1_q50),
    .col51(shift_register_1_q51), .col52(shift_register_1_q52), .col53(shift_register_1_q53),
    .col54(shift_register_1_q54), .col55(shift_register_1_q55), .col56(shift_register_1_q56),
    .col57(shift_register_1_q57), .col58(shift_register_1_q58), .col59(shift_register_1_q59),
    .col60(shift_register_1_q60), .col61(shift_register_1_q61), .col62(shift_register_1_q62),
    .col63(shift_register_1_out));
  or or_2 (rst, por_1_out, rst_out);
  buf buffer_5 (buffer_5_out, buffer_4_out);
  buf buffer_6 (data, buffer_5_out);
  EPROM_morse_transmitter eprom_morse_transmitter_1 (
    .clk(clk8), .char_available(keyboard_1_avail), .parallel_in({1'b0, keyboard_1_data}), .rst(rst),
    .load_next_char(eprom_morse_transmitter_1_load_next_char), .serial_out(morse));
  Pull_Resistor pull_resistor_1 (.node({pull_resistor_1_node_2[7], pull_resistor_1_node}));
  assign {pull_resistor_1_node_2[7], pull_resistor_1_node} = not_2_out ? MORSE_RECEIVER_ROM_data : 8'bz;  // Controlled_Buffer controlled_buffer_1
  not not_2 (not_2_out, rst);
  Counter #(.max('h6), .ongoal("stay"), .width(3)) counter_3 (
    .load(rst), .D(3'b110), .carry(char_received), .clk(clk8), .clr(morse));  // open: count, Q, up
  T_Flip_Flop t_ff_1 (.clk(clk1), .T(1'b1), .Q(t_ff_1_q));  // open: Qn, preset, reset
  // Probe on pull_resistor_1_node[5:0]
  T_Flip_Flop t_ff_2 (.clk(t_ff_1_q), .T(1'b1), .Q(t_ff_2_q));  // open: Qn, preset, reset
  T_Flip_Flop t_ff_3 (.clk(t_ff_2_q), .T(1'b1), .Q(t_ff_3_q[5]));  // open: Qn, preset, reset
  // Probe on multiplexer_1_out[4:0]
  ROM #(.addrWidth(15)) SERIAL_TRANSMITTER_ROM (
    .addr({1'b1, pull_resistor_1_node[5:0], word_received, char_received, t_ff_3_q[5], multiplexer_1_out[4:0]}),
    .data(SERIAL_TRANSMITTER_ROM_data));
  EPROM_uart_receiver eprom_uart_receiver_1 (
    .rst(rst), .clk(clk1), .serial_in(serial), .data_out(eprom_uart_receiver_1_data_out),
    .data_ready(eprom_uart_receiver_1_data_ready), .framing_error(eprom_uart_receiver_1_framing_error),
    .parity_error(eprom_uart_receiver_1_parity_error));
  LED led_1 (.in(eprom_uart_receiver_1_framing_error));
  LED led_2 (.in(eprom_uart_receiver_1_parity_error));
  Counter #(.max('hf), .ongoal("stay"), .width(4)) counter_4 (
    .load(rst), .D(4'b1111), .carry(word_received), .clk(clk8), .clr(morse));  // open: count, Q, up
  TTY tty_1 (
    .data(eprom_uart_receiver_1_data_out[6:0]), .clk(eprom_uart_receiver_1_data_ready), .clr(or_3_out));  // open: we
  or or_3 (or_3_out, button_2_out, rst);
  Button button_2 (.out(button_2_out));
  Multiplexer #(.enable("false"), .width(8)) multiplexer_1 (
    .in0(SERIAL_TRANSMITTER_ROM_data), .in1(8'h50), .out({reset_state, serial, multiplexer_1_out}), .sel(rst));

  // Other names for the same wires on the sheet: sclk = clk1; mclk = clk8

  // Notes on the sheet:
  //   contents of MORSE_RECEIVER_ROM (hex, n*v repeats v):
  //   54 61 62 6c 65 20 4f 66 20 43 6f 6e 74 65 6e 74 73 3a a a 53 74 61 72 74 20 28 62 69 6e 29 6*20 28
  //   68 65 78 29 20 20 45 6e 64 20 20 53 69 7a 65 a 15*30 2c 20 4*30 2c 20 2d 30 30 31 2c 20 4*30 20 3a
  //   20 54 61 62 6c 65 20 4f 66 20 43 6f 6e 74 65 6e 74 73 a 30 31 30 30 30 10*78 2c 20 32 30 30 30 2c 20
  //   32 33 66 66 2c 20 30 34 30 30 20 3a 20 4d 4f 52 53 45 5f 52 45 43 45 49 56 45 52 5f 52 4f 4d a 30 31
  //   30 30 31 30 30 8*78 2c 20 32 34 30 30 2c 20 32 34 66 66 2c 20 30 31 30 30 20 3a 20 4d 4f 52 53 45 5f
  //   54 52 41 4e 53 4d 49 54 54 45 52 5f 52 4f 4d a 30 31 30 30 31 30 31 8*78 2c 20 32 35 30 30 2c 20 32
  //   35 66 66 2c 20 30 31 30 30 20 3a 20 61 73 63 69 69 54 6f 4d 6f 72 73 65 54 72 61 6e 73 6d 69 74 74
  //   65 72 53 74 61 74 65 a 30 31 30 30 31 31 30 8*78 2c 20 32 36 30 30 2c 20 32 36 66 66 2c 20 30 31 30
  //   30 20 3a 20 61 73 63 69 69 54 6f 4d 6f 72 73 65 52 65 63 65 69 76 65 72 53 74 61 74 65 a 30 31 30 30
  //   31 31 31 30 30 6*78 2c 20 32 37 30 30 2c 20 32 37 33 66 2c 20 30 30 34 30 20 3a 20 6d 6f 72 73 65 52
  //   65 63 65 69 76 65 72 53 74 61 74 65 54 6f 41 73 63 69 69 a 30 31 30 30 31 31 31 30 31 6*78 2c 20 32
  //   37 34 30 2c 20 32 37 37 66 2c 20 30 30 34 30 20 3a 20 6d 6f 72 73 65 52 65 63 65 69 76 65 72 53 74
  //   61 74 65 54 6f 4e 6f 64 65 69 64 a 30 31 30 30 4*31 30 6*78 2c 20 32 37 38 30 2c 20 32 37 62 66 2c
  //   20 30 30 34 30 20 3a 20 6d 6f 72 73 65 52 65 63 65 69 76 65 72 53 74 61 74 65 54 6f 52 65 76 65 72
  //   73 65 64 4e 6f 64 65 69 64 a 30 31 30 31 30 10*78 2c 20 32 38 30 30 2c 20 32 62 66 66 2c 20 30 34 30
  //   30 20 3a 20 55 50 5f 44 4f 57 4e 5f 43 4f 55 4e 54 45 52 5f 52 4f 4d a 30 31 30 31 31 10*78 2c 20 32
  //   63 30 30 2c 20 32 66 66 66 2c 20 30 34 30 30 20 3a 20 6f 73 63 69 6c 6c 61 74 6f 72 73 a 30 31 31
  //   4*30 8*78 2c 20 33 30 30 30 2c 20 33 30 66 66 2c 20 30 31 30 30 20 3a 20 49 6e 74 54 6f 47 72 61 79
  //   a 30 31 31 30 30 30 31 8*78 2c 20 33 31 30 30 2c 20 33 31 66 66 2c 20 30 31 30 30 20 3a 20 47 72 61
  //   79 54 6f 49 6e 74 a 31 14*78 2c 20 34 30 30 30 2c 20 37 66 66 66 2c 20 34 30 30 30 20 3a 20 53 45 52
  //   49 41 4c 5f 54 52 41 4e 53 4d 49 54 54 45 52 5f 52 4f 4d a a a 44 65 74 61 69 6c 65 64 20 44 65 73
  //   63 72 69 70 74 69 6f 6e 3a a a 15*30 2c 20 4*30 2c 20 2d 30 30 31 2c 20 4*30 20 3a 20 54 61 62 6c 65
  //   20 4f 66 20 43 6f 6e 74 65 6e 74 73 a 30 31 30 30 30 10*78 2c 20 32 30 30 30 2c 20 32 33 66 66 2c 20
  //   30 34 30 30 20 3a 20 4d 4f 52 53 45 5f 52 45 43 45 49 56 45 52 5f 52 4f 4d a 20 20 41 6e 20 45 70 72
  //   6f 6d 20 53 74 61 74 65 20 4d 61 63 68 69 6e 65 20 74 68 61 74 20 72 65 63 65 69 76 65 73 20 73 65
  //   72 69 61 6c 20 6d 6f 72 73 65 20 63 6f 64 65 2e a 20 20 49 2f 4f 3a a 20 20 41 30 20 2e 2e 20 41 36
  //   2c 20 44 30 2e 2e 44 36 3a 20 73 74 61 74 65 20 28 36 20 73 74 61 74 65 20 62 69 74 73 20 28 36 34
  //   20 73 74 61 74 65 73 29 20 2b 20 31 20 70 61 72 69 74 79 20 62 69 74 29 a 20 20 41 37 3a 20 63 6c 6b
  //   20 28 73 65 72 69 61 6c 20 6d 6f 72 73 65 20 69 6e 70 75 74 29 a 20 20 41 38 3a 20 64 61 74 61 20 28
  //   64 65 6c 61 79 65 64 20 6d 6f 72 73 65 20 73 69 67 6e 61 6c 2c 20 73 61 6d 70 6c 65 64 20 61 74 20
  //   66 61 6c 6c 69 6e 67 20 65 64 67 65 20 6f 66 20 74 68 65 20 6d 6f 72 73 65 20 70 75 6c 73 65 2e 20
  //   30 20 66 6f 72 20 64 6f 74 2c 20 31 20 66 6f 72 20 64 61 73 68 29 a 20 20 41 39 3a 20 72 65 73 65 74
  //   20 28 73 65 74 73 20 74 68 65 20 73 74 61 74 65 20 30 29 a 20 20 44 37 3a 20 72 65 73 65 74 20 63 6f
  //   6d 70 6c 65 74 65 20 28 73 74 61 74 65 3d 3d 30 2c 20 72 65 61 64 79 20 74 6f 20 72 65 63 65 69 76
  //   65 20 74 68 65 20 6e 65 78 74 20 6d 6f 72 73 65 20 63 6f 64 65 29 a 20 20 a 30 31 30 30 31 30 30
  //   8*78 2c 20 32 34 30 30 2c 20 32 34 66 66 2c 20 30 31 30 30 20 3a 20 4d 4f 52 53 45 5f 54 52 41 4e 53
  //   4d 49 54 54 45 52 5f 52 4f 4d a 20 20 45 50 52 4f 4d 20 53 74 61 74 65 20 4d 61 63 68 69 6e 65 20 74
  //   68 61 74 20 67 65 6e 65 72 61 74 65 73 20 61 20 73 65 72 69 61 6c 20 4d 6f 72 73 65 20 6f 75 74 70
  //   75 74 20 66 6f 72 20 61 6e 20 69 6e 69 74 69 61 6c 20 69 6e 70 75 74 20 73 74 61 74 65 2a 2e a 20 20
  //   41 30 2e 2e 41 36 2c 44 30 2e 2e 44 36 3a 20 73 74 61 74 65 20 6f 66 20 74 68 65 20 73 74 61 74 65 2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
  //   contents of SERIAL_TRANSMITTER_ROM (hex, n*v repeats v):
  //   54 61 62 6c 65 20 4f 66 20 43 6f 6e 74 65 6e 74 73 3a a a 53 74 61 72 74 20 28 62 69 6e 29 6*20 28
  //   68 65 78 29 20 20 45 6e 64 20 20 53 69 7a 65 a 15*30 2c 20 4*30 2c 20 2d 30 30 31 2c 20 4*30 20 3a
  //   20 54 61 62 6c 65 20 4f 66 20 43 6f 6e 74 65 6e 74 73 a 30 31 30 30 30 10*78 2c 20 32 30 30 30 2c 20
  //   32 33 66 66 2c 20 30 34 30 30 20 3a 20 4d 4f 52 53 45 5f 52 45 43 45 49 56 45 52 5f 52 4f 4d a 30 31
  //   30 30 31 30 30 8*78 2c 20 32 34 30 30 2c 20 32 34 66 66 2c 20 30 31 30 30 20 3a 20 4d 4f 52 53 45 5f
  //   54 52 41 4e 53 4d 49 54 54 45 52 5f 52 4f 4d a 30 31 30 30 31 30 31 8*78 2c 20 32 35 30 30 2c 20 32
  //   35 66 66 2c 20 30 31 30 30 20 3a 20 61 73 63 69 69 54 6f 4d 6f 72 73 65 54 72 61 6e 73 6d 69 74 74
  //   65 72 53 74 61 74 65 a 30 31 30 30 31 31 30 8*78 2c 20 32 36 30 30 2c 20 32 36 66 66 2c 20 30 31 30
  //   30 20 3a 20 61 73 63 69 69 54 6f 4d 6f 72 73 65 52 65 63 65 69 76 65 72 53 74 61 74 65 a 30 31 30 30
  //   31 31 31 30 30 6*78 2c 20 32 37 30 30 2c 20 32 37 33 66 2c 20 30 30 34 30 20 3a 20 6d 6f 72 73 65 52
  //   65 63 65 69 76 65 72 53 74 61 74 65 54 6f 41 73 63 69 69 a 30 31 30 30 31 31 31 30 31 6*78 2c 20 32
  //   37 34 30 2c 20 32 37 37 66 2c 20 30 30 34 30 20 3a 20 6d 6f 72 73 65 52 65 63 65 69 76 65 72 53 74
  //   61 74 65 54 6f 4e 6f 64 65 69 64 a 30 31 30 30 4*31 30 6*78 2c 20 32 37 38 30 2c 20 32 37 62 66 2c
  //   20 30 30 34 30 20 3a 20 6d 6f 72 73 65 52 65 63 65 69 76 65 72 53 74 61 74 65 54 6f 52 65 76 65 72
  //   73 65 64 4e 6f 64 65 69 64 a 30 31 30 31 30 10*78 2c 20 32 38 30 30 2c 20 32 62 66 66 2c 20 30 34 30
  //   30 20 3a 20 55 50 5f 44 4f 57 4e 5f 43 4f 55 4e 54 45 52 5f 52 4f 4d a 30 31 30 31 31 10*78 2c 20 32
  //   63 30 30 2c 20 32 66 66 66 2c 20 30 34 30 30 20 3a 20 6f 73 63 69 6c 6c 61 74 6f 72 73 a 30 31 31
  //   4*30 8*78 2c 20 33 30 30 30 2c 20 33 30 66 66 2c 20 30 31 30 30 20 3a 20 49 6e 74 54 6f 47 72 61 79
  //   a 30 31 31 30 30 30 31 8*78 2c 20 33 31 30 30 2c 20 33 31 66 66 2c 20 30 31 30 30 20 3a 20 47 72 61
  //   79 54 6f 49 6e 74 a 31 14*78 2c 20 34 30 30 30 2c 20 37 66 66 66 2c 20 34 30 30 30 20 3a 20 53 45 52
  //   49 41 4c 5f 54 52 41 4e 53 4d 49 54 54 45 52 5f 52 4f 4d a a a 44 65 74 61 69 6c 65 64 20 44 65 73
  //   63 72 69 70 74 69 6f 6e 3a a a 15*30 2c 20 4*30 2c 20 2d 30 30 31 2c 20 4*30 20 3a 20 54 61 62 6c 65
  //   20 4f 66 20 43 6f 6e 74 65 6e 74 73 a 30 31 30 30 30 10*78 2c 20 32 30 30 30 2c 20 32 33 66 66 2c 20
  //   30 34 30 30 20 3a 20 4d 4f 52 53 45 5f 52 45 43 45 49 56 45 52 5f 52 4f 4d a 20 20 41 6e 20 45 70 72
  //   6f 6d 20 53 74 61 74 65 20 4d 61 63 68 69 6e 65 20 74 68 61 74 20 72 65 63 65 69 76 65 73 20 73 65
  //   72 69 61 6c 20 6d 6f 72 73 65 20 63 6f 64 65 2e a 20 20 49 2f 4f 3a a 20 20 41 30 20 2e 2e 20 41 36
  //   2c 20 44 30 2e 2e 44 36 3a 20 73 74 61 74 65 20 28 36 20 73 74 61 74 65 20 62 69 74 73 20 28 36 34
  //   20 73 74 61 74 65 73 29 20 2b 20 31 20 70 61 72 69 74 79 20 62 69 74 29 a 20 20 41 37 3a 20 63 6c 6b
  //   20 28 73 65 72 69 61 6c 20 6d 6f 72 73 65 20 69 6e 70 75 74 29 a 20 20 41 38 3a 20 64 61 74 61 20 28
  //   64 65 6c 61 79 65 64 20 6d 6f 72 73 65 20 73 69 67 6e 61 6c 2c 20 73 61 6d 70 6c 65 64 20 61 74 20
  //   66 61 6c 6c 69 6e 67 20 65 64 67 65 20 6f 66 20 74 68 65 20 6d 6f 72 73 65 20 70 75 6c 73 65 2e 20
  //   30 20 66 6f 72 20 64 6f 74 2c 20 31 20 66 6f 72 20 64 61 73 68 29 a 20 20 41 39 3a 20 72 65 73 65 74
  //   20 28 73 65 74 73 20 74 68 65 20 73 74 61 74 65 20 30 29 a 20 20 44 37 3a 20 72 65 73 65 74 20 63 6f
  //   6d 70 6c 65 74 65 20 28 73 74 61 74 65 3d 3d 30 2c 20 72 65 61 64 79 20 74 6f 20 72 65 63 65 69 76
  //   65 20 74 68 65 20 6e 65 78 74 20 6d 6f 72 73 65 20 63 6f 64 65 29 a 20 20 a 30 31 30 30 31 30 30
  //   8*78 2c 20 32 34 30 30 2c 20 32 34 66 66 2c 20 30 31 30 30 20 3a 20 4d 4f 52 53 45 5f 54 52 41 4e 53
  //   4d 49 54 54 45 52 5f 52 4f 4d a 20 20 45 50 52 4f 4d 20 53 74 61 74 65 20 4d 61 63 68 69 6e 65 20 74
  //   68 61 74 20 67 65 6e 65 72 61 74 65 73 20 61 20 73 65 72 69 61 6c 20 4d 6f 72 73 65 20 6f 75 74 70
  //   75 74 20 66 6f 72 20 61 6e 20 69 6e 69 74 69 61 6c 20 69 6e 70 75 74 20 73 74 61 74 65 2a 2e a 20 20
  //   41 30 2e 2e 41 36 2c 44 30 2e 2e 44 36 3a 20 73 74 61 74 65 20 6f 66 20 74 68 65 20 73 74 61 74 65 2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
endmodule

module morse_transmitter (
  input  clk,
  input  char_available,
  input  [7:0] parallel_in,
  input  rst,
  output load_next_char,
  output serial_out
);

  wire and_1_out, bit_ready, buffer_1_out, buffer_2_out, buffer_3_out, buffer_4_out, buffer_5_out,
       buffer_6_out, buffer_7_out, buffer_8_out, buffer_10_out, buffer_11_out, buffer_12_out, buffer_13_out,
       buffer_14_out, buffer_15_out, buffer_16_out, buffer_17_out, buffer_18_out, buffer_19_out,
       buffer_20_out, buffer_21_out, buffer_22_out, buffer_23_out, buffer_24_out, buffer_25_out,
       counter_1_carry, counter_2_carry, counter_3_carry, counter_4_carry, counter_5_carry, dash, dot,
       not_1_out, not_2_out, or_1_out, shift_bits, shift_register_1_q0, shift_register_1_q1,
       shift_register_1_q2, shift_register_1_q3, shift_register_1_q4, shift_register_1_q5,
       shift_register_1_q6, shifter_empty, shifter_not_empty, space, transmitter_idle;
  wire [0:0] shift_register_1_out;
  wire [7:0] Morse_Codes_data;

  ROM Morse_Codes (.addr(parallel_in), .data(Morse_Codes_data));
  buf buffer_1 (buffer_1_out, shifter_empty);
  buf buffer_2 (buffer_2_out, buffer_5_out);
  buf buffer_3 (buffer_3_out, buffer_2_out);
  buf buffer_4 (buffer_4_out, buffer_3_out);
  buf buffer_5 (buffer_5_out, buffer_1_out);
  or or_1 (or_1_out, shift_bits, load_next_char);
  buf buffer_6 (buffer_6_out, buffer_7_out);
  buf buffer_7 (buffer_7_out, buffer_17_out);
  buf buffer_8 (buffer_8_out, buffer_6_out);
  buf buffer_9 (bit_ready, buffer_8_out);
  buf buffer_10 (buffer_10_out, buffer_4_out);
  buf buffer_11 (buffer_11_out, buffer_10_out);
  buf buffer_12 (buffer_12_out, buffer_11_out);
  buf buffer_13 (buffer_13_out, buffer_12_out);
  buf buffer_14 (buffer_14_out, char_available);
  buf buffer_15 (buffer_15_out, buffer_14_out);
  buf buffer_16 (buffer_16_out, buffer_15_out);
  not not_1 (not_1_out, or_1_out);
  and and_1 (and_1_out, not_1_out, or_1_out);
  buf buffer_17 (buffer_17_out, buffer_18_out);
  buf buffer_18 (buffer_18_out, and_1_out);
  buf buffer_19 (buffer_19_out, buffer_13_out);
  buf buffer_20 (buffer_20_out, buffer_19_out);
  buf buffer_21 (buffer_21_out, buffer_20_out);
  buf buffer_22 (buffer_22_out, buffer_21_out);
  buf buffer_23 (buffer_23_out, buffer_16_out);
  buf buffer_24 (buffer_24_out, buffer_23_out);
  buf buffer_25 (buffer_25_out, buffer_24_out);
  and and_2 (shift_bits, shifter_not_empty, transmitter_idle);
  // Probe on Morse_Codes_data
  not not_2 (not_2_out, shifter_not_empty);
  Shift_Register shift_register_1 (
    .shift(shifter_not_empty), .in(1'b0), .clk(and_1_out), .out(shift_register_1_out[0]), .load(not_2_out),
    .clr(rst), .d0(Morse_Codes_data[7]), .q0(shift_register_1_q0), .d1(Morse_Codes_data[6]),
    .q1(shift_register_1_q1), .d2(Morse_Codes_data[5]), .q2(shift_register_1_q2), .d3(Morse_Codes_data[4]),
    .q3(shift_register_1_q3), .d4(Morse_Codes_data[3]), .q4(shift_register_1_q4), .d5(Morse_Codes_data[2]),
    .q5(shift_register_1_q5), .d6(Morse_Codes_data[1]), .q6(shift_register_1_q6), .d7(Morse_Codes_data[0]));  // open: q7
  not not_3 (shifter_empty, shifter_not_empty);
  and and_3 (load_next_char, buffer_22_out, buffer_25_out, transmitter_idle);
  or or_2 (shifter_not_empty, shift_register_1_q0, shift_register_1_q1, shift_register_1_q2, shift_register_1_q3, shift_register_1_q4, shift_register_1_q5, shift_register_1_q6);
  Demultiplexer #(.enable("false"), .select(2)) demultiplexer_1 (
    .out1(space), .out2(dot), .out3(dash), .in(bit_ready), .sel({shifter_not_empty, shift_register_1_out[0]}));  // open: out0
  Counter #(.max('h3), .ongoal("stay")) counter_1 (
    .load(rst), .D(8'h3), .carry(counter_1_carry), .clk(clk), .clr(dot));  // open: count, Q, up
  Counter #(.max('hb), .ongoal("stay")) counter_2 (
    .load(rst), .D(8'hb), .carry(counter_2_carry), .clk(clk), .clr(dash));  // open: count, Q, up
  Counter #(.max('hb), .ongoal("stay")) counter_3 (
    .load(rst), .D(8'hb), .carry(counter_3_carry), .clk(clk), .clr(space));  // open: count, Q, up
  Counter #(.max('h3), .ongoal("stay")) counter_4 (
    .load(rst), .D(8'h3), .count(counter_1_carry), .carry(counter_4_carry), .clk(clk), .clr(dot));  // open: Q, up
  Counter #(.max('h3), .ongoal("stay")) counter_5 (
    .load(rst), .D(8'h3), .count(counter_2_carry), .carry(counter_5_carry), .clk(clk), .clr(dash));  // open: Q, up
  or or_3 (serial_out, ~counter_1_carry, ~counter_2_carry);  // OR_Gate
  and and_4 (transmitter_idle, counter_4_carry, counter_5_carry, counter_3_carry);

  // Notes on the sheet:
  //   contents of Morse_Codes (hex, n*v repeats v):
  //   32*0 1 67 52 0 0 0 22 5e 2d 6d 0 2a 73 61 6a 29 3f 3e 3c 38 30 20 21 23 27 2f 47 35 0 31 0 4c 56 6
  //   11 15 9 2 14 b 10 4 1e d 12 7 5 f 16 1b a 8 3 c 18 e 19 1d 13 0 39 0 0 6c 0 6 11 15 9 2 14 b 10 4 1e
  //   d 12 7 5 f 16 1b a 8 3 c 18 e 19 1d 13 69*0 36 0 0 0 1a 0 0 0 32 24 6*0 2c 5*0 17 5*0 1c 0 0 0 36 0
  //   0 0 1a 0 0 0 32 24 6*0 2c 5*0 17 5*0 1c
endmodule

module morse_receiver (
  input  rst,
  input  clk,
  input  morse_in,
  output [7:0] parallel_out,
  output data_ready,
  output [3:0] diagnostic_out
);

  wire and_1_out, and_2_out, buffer_1_out, buffer_2_out, buffer_3_out, buffer_4_out, buffer_5_out,
       buffer_6_out, buffer_7_out, buffer_8_out, buffer_9_out, buffer_10_out, buffer_11_out, buffer_12_out,
       buffer_13_out, buffer_14_out, buffer_15_out, buffer_16_out, buffer_17_out, buffer_18_out,
       buffer_19_out, buffer_20_out, buffer_21_out, buffer_22_out, buffer_23_out, buffer_24_out,
       buffer_25_out, buffer_26_out, buffer_27_out, buffer_28_out, nor_1_out, nor_2_out, not_1_out,
       not_2_out, not_3_out, not_4_out, not_5_out, not_6_out, or_1_out, shift_register_1_out;
  wire [6:0] shift_register_1_q0;

  Counter #(.max('h6), .ongoal("stay"), .width(3)) counter_1 (
    .load(rst), .D(3'b110), .carry(diagnostic_out[1]), .clk(clk), .clr(morse_in));  // open: count, Q, up
  Counter #(.max('h8), .ongoal("stay"), .width(4)) counter_2 (
    .load(rst), .D(4'b1000), .count(diagnostic_out[1]), .carry(diagnostic_out[0]), .clk(clk), .clr(morse_in));  // open: Q, up
  Counter #(.max('h5), .ongoal("stay"), .width(3)) counter_3 (
    .carry(diagnostic_out[2]), .clk(clk), .clr(not_1_out));  // open: load, D, count, Q, up
  not not_1 (not_1_out, morse_in);
  not not_2 (not_2_out, diagnostic_out[0]);
  not not_3 (not_3_out, diagnostic_out[1]);
  buf buffer_1 (buffer_1_out, diagnostic_out[2]);
  buf buffer_2 (buffer_2_out, buffer_1_out);
  buf buffer_3 (buffer_3_out, buffer_2_out);
  not not_4 (not_4_out, diagnostic_out[1]);
  buf buffer_4 (buffer_4_out, diagnostic_out[1]);
  buf buffer_5 (buffer_5_out, buffer_4_out);
  and and_1 (and_1_out, not_2_out, diagnostic_out[0]);
  buf buffer_6 (buffer_6_out, and_1_out);
  and and_2 (and_2_out, not_3_out, diagnostic_out[1]);
  buf buffer_7 (buffer_7_out, buffer_3_out);
  buf buffer_8 (buffer_8_out, buffer_7_out);
  buf buffer_9 (buffer_9_out, buffer_8_out);
  nor nor_1 (nor_1_out, morse_in, not_5_out);
  not not_5 (not_5_out, morse_in);
  nor nor_2 (nor_2_out, not_4_out, diagnostic_out[1]);
  buf buffer_10 (buffer_10_out, buffer_5_out);
  buf buffer_11 (buffer_11_out, buffer_10_out);
  buf buffer_12 (buffer_12_out, buffer_11_out);
  buf buffer_13 (buffer_13_out, buffer_6_out);
  buf buffer_14 (buffer_14_out, buffer_13_out);
  buf buffer_15 (buffer_15_out, buffer_14_out);
  buf buffer_16 (buffer_16_out, buffer_15_out);
  or or_1 (or_1_out, nor_1_out, nor_2_out, and_1_out);
  buf buffer_17 (buffer_17_out, buffer_12_out);
  buf buffer_18 (buffer_18_out, buffer_16_out);
  buf buffer_19 (buffer_19_out, buffer_18_out);
  buf buffer_20 (buffer_20_out, buffer_19_out);
  buf buffer_21 (buffer_21_out, buffer_20_out);
  not not_6 (not_6_out, buffer_17_out);
  Shift_Register shift_register_1 (
    .shift(not_6_out), .in(buffer_9_out), .clk(or_1_out), .out(shift_register_1_out), .load(buffer_17_out),
    .clr(rst), .d0(1'b1), .q0(shift_register_1_q0[0]), .d1(1'b0), .q1(shift_register_1_q0[1]), .d2(1'b0),
    .q2(shift_register_1_q0[2]), .d3(1'b0), .q3(shift_register_1_q0[3]), .d4(1'b0),
    .q4(shift_register_1_q0[4]), .d5(1'b0), .q5(shift_register_1_q0[5]), .d6(1'b0),
    .q6(shift_register_1_q0[6]), .d7(1'b0), .q7(shift_register_1_out));
  buf buffer_22 (buffer_22_out, buffer_21_out);
  buf buffer_23 (buffer_23_out, buffer_22_out);
  buf buffer_24 (buffer_24_out, buffer_23_out);
  buf buffer_25 (buffer_25_out, buffer_24_out);
  ROM #(.addrWidth(7)) rom_1 (.addr(shift_register_1_q0), .data(parallel_out));
  buf buffer_26 (buffer_26_out, buffer_25_out);
  buf buffer_27 (buffer_27_out, buffer_26_out);
  buf buffer_28 (buffer_28_out, buffer_27_out);
  or or_2 (data_ready, buffer_28_out, and_2_out);

  assign diagnostic_out[3] = morse_in;

  // Notes on the sheet:
  //   contents of rom_1 (hex, n*v repeats v):
  //   0 20 65 74 69 61 6e 6d 73 75 72 77 64 6b 67 6f 68 76 66 fc 6c e4 70 6a 62 78 63 79 7a 71 f6 20 35 34
  //   0 33 e9 0 f0 32 26 e8 2b 0 0 e0 0 31 36 3d 2f 5c 0 3b 28 0 37 20 0 0 38 0 39 30 12*0 3f 5f 4*0 22 0
  //   0 2e 4*0 40 0 0 0 27 0 0 2d 11*0 29 5*0 2c 4*0 3a 21 d1 a8 9d d2 25 31
endmodule

module uart_receiver (
  input  rst,
  input  clk,
  input  serial_in,
  output [7:0] data_out,
  output data_ready,
  output framing_error,
  output parity_error
);

  wire and_1_out, bitselector_1_out, counter_1_carry, odd_parity_1_out, or_1_out, shift_register_1_out,
       shift_register_1_q0, shift_register_1_q1, xor_1_out;
  wire [7:0] counter_1_q;

  and and_1 (and_1_out, ~serial_in, counter_1_carry);  // AND_Gate
  BitSelector bitselector_1 (.in(counter_1_q), .out(bitselector_1_out), .sel(3'b001));
  Counter #(.max('h2c), .ongoal("stay")) counter_1 (
    .load(rst), .D(8'h2c), .Q(counter_1_q), .carry(counter_1_carry), .clk(clk), .clr(and_1_out));  // open: count, up
  Shift_Register #(.length(11)) shift_register_1 (
    .in(serial_in), .clk(bitselector_1_out), .out(shift_register_1_out), .clr(rst), .q0(shift_register_1_q0),
    .q1(shift_register_1_q1), .q2(data_out[7]), .q3(data_out[6]), .q4(data_out[5]), .q5(data_out[4]),
    .q6(data_out[3]), .q7(data_out[2]), .q8(data_out[1]), .q9(data_out[0]));  // open: shift, load, d0, d1, d2, d3, d4, d5, d6, d7, d8, d9, d10, q10
  xor odd_parity_1 (odd_parity_1_out, data_out[0], data_out[1], data_out[2], data_out[3], data_out[4], data_out[5], data_out[6], data_out[7]);
  ExactlyOne xor_1 (.out(xor_1_out), .in0(1'b1), .in1(shift_register_1_q1), .in2(odd_parity_1_out));
  or or_1 (or_1_out, ~shift_register_1_q0, shift_register_1_out);  // OR_Gate
  and and_2 (framing_error, counter_1_carry, or_1_out);
  and and_3 (parity_error, counter_1_carry, xor_1_out);
  and and_4 (data_ready, counter_1_carry, ~framing_error, ~parity_error);  // AND_Gate
endmodule

module uart_transmitter (
  input  rst,
  input  clk,
  input  input_availlable,
  input  [7:0] parallel_in,
  output next_input,
  output serial_out
);

  wire and_1_out, buffer_1_out, buffer_2_out, buffer_3_out, buffer_4_out, buffer_5_out, buffer_7_out,
       buffer_8_out, buffer_10_out, buffer_11_out, j_k_ff_1_q, j_k_ff_1_qn, load, not_1_out,
       odd_parity_1_out, or_1_out, or_2_out, set_load, shift, shift_register_1_out, start_transmission,
       transmitter_idle, xor_1_out;
  wire [7:0] counter_1_q;

  Counter #(.max('h30), .ongoal("stay")) counter_1 (
    .load(rst), .D(8'h30), .Q(counter_1_q), .carry(transmitter_idle), .clk(clk), .clr(start_transmission));  // open: count, up
  BitSelector bitselector_1 (.in(counter_1_q), .out(shift), .sel(3'b001));
  J_K_Flip_Flop j_k_ff_1 (.Q(j_k_ff_1_q), .Qn(j_k_ff_1_qn), .preset(next_input), .reset(or_1_out));  // open: J, clk, K
  or or_1 (or_1_out, set_load, rst);
  or or_2 (or_2_out, load, shift);
  not not_1 (not_1_out, and_1_out);
  and and_1 (and_1_out, input_availlable, transmitter_idle);
  xor odd_parity_1 (odd_parity_1_out, parallel_in[0], parallel_in[1], parallel_in[2], parallel_in[3], parallel_in[4], parallel_in[5], parallel_in[6], parallel_in[7]);
  xor xor_1 (xor_1_out, 1'b1, odd_parity_1_out);
  Shift_Register #(.length(12)) shift_register_1 (
    .shift(j_k_ff_1_q), .in(1'b1), .clk(or_2_out), .out(shift_register_1_out), .load(j_k_ff_1_qn), .clr(rst),
    .d0(1'b1), .d1(xor_1_out), .d2(parallel_in[7]), .d3(parallel_in[6]), .d4(parallel_in[5]),
    .d5(parallel_in[4]), .d6(parallel_in[3]), .d7(parallel_in[2]), .d8(parallel_in[1]), .d9(parallel_in[0]),
    .d10(1'b0), .d11(1'b1));  // open: q0, q1, q2, q3, q4, q5, q6, q7, q8, q9, q10, q11
  and and_2 (set_load, not_1_out, and_1_out);
  buf buffer_1 (buffer_1_out, set_load);
  buf buffer_2 (buffer_2_out, buffer_1_out);
  buf buffer_3 (buffer_3_out, buffer_2_out);
  buf buffer_4 (buffer_4_out, buffer_3_out);
  buf buffer_5 (buffer_5_out, buffer_4_out);
  buf buffer_6 (load, buffer_5_out);
  buf buffer_7 (buffer_7_out, load);
  or or_3 (serial_out, shift_register_1_out, transmitter_idle);
  buf buffer_8 (buffer_8_out, buffer_7_out);
  buf buffer_9 (next_input, buffer_8_out);
  buf buffer_10 (buffer_10_out, next_input);
  buf buffer_11 (buffer_11_out, buffer_10_out);
  buf buffer_12 (start_transmission, buffer_11_out);

  // Other names for the same wires on the sheet: input_available = input_availlable; set_shift = next_input
endmodule

module EPROM_morse_transmitter (
  input  clk,
  input  char_available,
  input  [7:0] parallel_in,
  input  rst,
  output load_next_char,
  output serial_out
);

  wire buffer_1_out, buffer_2_out, buffer_3_out, buffer_4_out, buffer_5_out, buffer_6_out, counter_1_carry,
       not_OE_out, or_1_out, transmitter_idle;
  wire [6:0] MORSE_ROM_STATE_MACHINE_data, multiplexer_1_out;
  wire [7:0] MORSE_ROM_ASCII_LOOKUP_data;
  wire [7:7] MORSE_ROM_STATE_MACHINE_data_2, t_ff_1_q;

  ROM #(.addrWidth(15)) MORSE_ROM_ASCII_LOOKUP (.addr({7'b0100101, parallel_in}), .data(MORSE_ROM_ASCII_LOOKUP_data));
  buf buffer_1 (buffer_1_out, char_available);
  buf buffer_2 (buffer_2_out, buffer_1_out);
  buf buffer_3 (buffer_3_out, buffer_2_out);
  buf buffer_4 (buffer_4_out, buffer_3_out);
  buf buffer_5 (buffer_5_out, buffer_4_out);
  buf buffer_6 (buffer_6_out, buffer_5_out);
  // Probe on MORSE_ROM_ASCII_LOOKUP_data[6:0]
  and and_1 (load_next_char, buffer_6_out, transmitter_idle);
  Multiplexer #(.enable("false"), .width(7)) multiplexer_1 (
    .in0(MORSE_ROM_STATE_MACHINE_data), .in1(MORSE_ROM_ASCII_LOOKUP_data[6:0]), .out(multiplexer_1_out),
    .sel(or_1_out));
  Counter #(.max('h3), .width(2)) counter_1 (
    .carry(counter_1_carry), .clk(clk), .clr(or_1_out));  // open: load, D, count, Q, up
  or or_1 (or_1_out, rst, load_next_char);
  // Probe on MORSE_ROM_STATE_MACHINE_data
  ROM #(.addrWidth(15)) MORSE_ROM_STATE_MACHINE (
    .addr({7'b0100100, t_ff_1_q[7], multiplexer_1_out}),
    .data({MORSE_ROM_STATE_MACHINE_data_2[7], MORSE_ROM_STATE_MACHINE_data}));
  T_Flip_Flop #(.trigger("falling")) t_ff_1 (
    .clk(counter_1_carry), .T(1'b1), .Q(t_ff_1_q[7]), .reset(or_1_out));  // open: Qn, preset
  Pull_Resistor pull_resistor_1 (.node(serial_out));
  assign serial_out = not_OE_out ? MORSE_ROM_STATE_MACHINE_data_2[7] : 1'bz;  // Controlled_Buffer controlled_buffer_1
  not not_OE (not_OE_out, or_1_out);
  nor nor_1 (transmitter_idle, MORSE_ROM_STATE_MACHINE_data[0], MORSE_ROM_STATE_MACHINE_data[1], MORSE_ROM_STATE_MACHINE_data[2], MORSE_ROM_STATE_MACHINE_data[3], MORSE_ROM_STATE_MACHINE_data[4], MORSE_ROM_STATE_MACHINE_data[5], MORSE_ROM_STATE_MACHINE_data[6]);

  // Notes on the sheet:
  //   contents of MORSE_ROM_ASCII_LOOKUP (hex, n*v repeats v):
  //   54 61 62 6c 65 20 4f 66 20 43 6f 6e 74 65 6e 74 73 3a a a 53 74 61 72 74 20 28 62 69 6e 29 6*20 28
  //   68 65 78 29 20 20 45 6e 64 20 20 53 69 7a 65 a 15*30 2c 20 4*30 2c 20 2d 30 30 31 2c 20 4*30 20 3a
  //   20 54 61 62 6c 65 20 4f 66 20 43 6f 6e 74 65 6e 74 73 a 30 31 30 30 30 10*78 2c 20 32 30 30 30 2c 20
  //   32 33 66 66 2c 20 30 34 30 30 20 3a 20 4d 4f 52 53 45 5f 52 45 43 45 49 56 45 52 5f 52 4f 4d a 30 31
  //   30 30 31 30 30 8*78 2c 20 32 34 30 30 2c 20 32 34 66 66 2c 20 30 31 30 30 20 3a 20 4d 4f 52 53 45 5f
  //   54 52 41 4e 53 4d 49 54 54 45 52 5f 52 4f 4d a 30 31 30 30 31 30 31 8*78 2c 20 32 35 30 30 2c 20 32
  //   35 66 66 2c 20 30 31 30 30 20 3a 20 61 73 63 69 69 54 6f 4d 6f 72 73 65 54 72 61 6e 73 6d 69 74 74
  //   65 72 53 74 61 74 65 a 30 31 30 30 31 31 30 8*78 2c 20 32 36 30 30 2c 20 32 36 66 66 2c 20 30 31 30
  //   30 20 3a 20 61 73 63 69 69 54 6f 4d 6f 72 73 65 52 65 63 65 69 76 65 72 53 74 61 74 65 a 30 31 30 30
  //   31 31 31 30 30 6*78 2c 20 32 37 30 30 2c 20 32 37 33 66 2c 20 30 30 34 30 20 3a 20 6d 6f 72 73 65 52
  //   65 63 65 69 76 65 72 53 74 61 74 65 54 6f 41 73 63 69 69 a 30 31 30 30 31 31 31 30 31 6*78 2c 20 32
  //   37 34 30 2c 20 32 37 37 66 2c 20 30 30 34 30 20 3a 20 6d 6f 72 73 65 52 65 63 65 69 76 65 72 53 74
  //   61 74 65 54 6f 4e 6f 64 65 69 64 a 30 31 30 30 4*31 30 6*78 2c 20 32 37 38 30 2c 20 32 37 62 66 2c
  //   20 30 30 34 30 20 3a 20 6d 6f 72 73 65 52 65 63 65 69 76 65 72 53 74 61 74 65 54 6f 52 65 76 65 72
  //   73 65 64 4e 6f 64 65 69 64 a 30 31 30 31 30 10*78 2c 20 32 38 30 30 2c 20 32 62 66 66 2c 20 30 34 30
  //   30 20 3a 20 55 50 5f 44 4f 57 4e 5f 43 4f 55 4e 54 45 52 5f 52 4f 4d a 30 31 30 31 31 10*78 2c 20 32
  //   63 30 30 2c 20 32 66 66 66 2c 20 30 34 30 30 20 3a 20 6f 73 63 69 6c 6c 61 74 6f 72 73 a 30 31 31
  //   4*30 8*78 2c 20 33 30 30 30 2c 20 33 30 66 66 2c 20 30 31 30 30 20 3a 20 49 6e 74 54 6f 47 72 61 79
  //   a 30 31 31 30 30 30 31 8*78 2c 20 33 31 30 30 2c 20 33 31 66 66 2c 20 30 31 30 30 20 3a 20 47 72 61
  //   79 54 6f 49 6e 74 a 31 14*78 2c 20 34 30 30 30 2c 20 37 66 66 66 2c 20 34 30 30 30 20 3a 20 53 45 52
  //   49 41 4c 5f 54 52 41 4e 53 4d 49 54 54 45 52 5f 52 4f 4d a a a 44 65 74 61 69 6c 65 64 20 44 65 73
  //   63 72 69 70 74 69 6f 6e 3a a a 15*30 2c 20 4*30 2c 20 2d 30 30 31 2c 20 4*30 20 3a 20 54 61 62 6c 65
  //   20 4f 66 20 43 6f 6e 74 65 6e 74 73 a 30 31 30 30 30 10*78 2c 20 32 30 30 30 2c 20 32 33 66 66 2c 20
  //   30 34 30 30 20 3a 20 4d 4f 52 53 45 5f 52 45 43 45 49 56 45 52 5f 52 4f 4d a 20 20 41 6e 20 45 70 72
  //   6f 6d 20 53 74 61 74 65 20 4d 61 63 68 69 6e 65 20 74 68 61 74 20 72 65 63 65 69 76 65 73 20 73 65
  //   72 69 61 6c 20 6d 6f 72 73 65 20 63 6f 64 65 2e a 20 20 49 2f 4f 3a a 20 20 41 30 20 2e 2e 20 41 36
  //   2c 20 44 30 2e 2e 44 36 3a 20 73 74 61 74 65 20 28 36 20 73 74 61 74 65 20 62 69 74 73 20 28 36 34
  //   20 73 74 61 74 65 73 29 20 2b 20 31 20 70 61 72 69 74 79 20 62 69 74 29 a 20 20 41 37 3a 20 63 6c 6b
  //   20 28 73 65 72 69 61 6c 20 6d 6f 72 73 65 20 69 6e 70 75 74 29 a 20 20 41 38 3a 20 64 61 74 61 20 28
  //   64 65 6c 61 79 65 64 20 6d 6f 72 73 65 20 73 69 67 6e 61 6c 2c 20 73 61 6d 70 6c 65 64 20 61 74 20
  //   66 61 6c 6c 69 6e 67 20 65 64 67 65 20 6f 66 20 74 68 65 20 6d 6f 72 73 65 20 70 75 6c 73 65 2e 20
  //   30 20 66 6f 72 20 64 6f 74 2c 20 31 20 66 6f 72 20 64 61 73 68 29 a 20 20 41 39 3a 20 72 65 73 65 74
  //   20 28 73 65 74 73 20 74 68 65 20 73 74 61 74 65 20 30 29 a 20 20 44 37 3a 20 72 65 73 65 74 20 63 6f
  //   6d 70 6c 65 74 65 20 28 73 74 61 74 65 3d 3d 30 2c 20 72 65 61 64 79 20 74 6f 20 72 65 63 65 69 76
  //   65 20 74 68 65 20 6e 65 78 74 20 6d 6f 72 73 65 20 63 6f 64 65 29 a 20 20 a 30 31 30 30 31 30 30
  //   8*78 2c 20 32 34 30 30 2c 20 32 34 66 66 2c 20 30 31 30 30 20 3a 20 4d 4f 52 53 45 5f 54 52 41 4e 53
  //   4d 49 54 54 45 52 5f 52 4f 4d a 20 20 45 50 52 4f 4d 20 53 74 61 74 65 20 4d 61 63 68 69 6e 65 20 74
  //   68 61 74 20 67 65 6e 65 72 61 74 65 73 20 61 20 73 65 72 69 61 6c 20 4d 6f 72 73 65 20 6f 75 74 70
  //   75 74 20 66 6f 72 20 61 6e 20 69 6e 69 74 69 61 6c 20 69 6e 70 75 74 20 73 74 61 74 65 2a 2e a 20 20
  //   41 30 2e 2e 41 36 2c 44 30 2e 2e 44 36 3a 20 73 74 61 74 65 20 6f 66 20 74 68 65 20 73 74 61 74 65 2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
  //   contents of MORSE_ROM_STATE_MACHINE (hex, n*v repeats v):
  //   54 61 62 6c 65 20 4f 66 20 43 6f 6e 74 65 6e 74 73 3a a a 53 74 61 72 74 20 28 62 69 6e 29 6*20 28
  //   68 65 78 29 20 20 45 6e 64 20 20 53 69 7a 65 a 15*30 2c 20 4*30 2c 20 2d 30 30 31 2c 20 4*30 20 3a
  //   20 54 61 62 6c 65 20 4f 66 20 43 6f 6e 74 65 6e 74 73 a 30 31 30 30 30 10*78 2c 20 32 30 30 30 2c 20
  //   32 33 66 66 2c 20 30 34 30 30 20 3a 20 4d 4f 52 53 45 5f 52 45 43 45 49 56 45 52 5f 52 4f 4d a 30 31
  //   30 30 31 30 30 8*78 2c 20 32 34 30 30 2c 20 32 34 66 66 2c 20 30 31 30 30 20 3a 20 4d 4f 52 53 45 5f
  //   54 52 41 4e 53 4d 49 54 54 45 52 5f 52 4f 4d a 30 31 30 30 31 30 31 8*78 2c 20 32 35 30 30 2c 20 32
  //   35 66 66 2c 20 30 31 30 30 20 3a 20 61 73 63 69 69 54 6f 4d 6f 72 73 65 54 72 61 6e 73 6d 69 74 74
  //   65 72 53 74 61 74 65 a 30 31 30 30 31 31 30 8*78 2c 20 32 36 30 30 2c 20 32 36 66 66 2c 20 30 31 30
  //   30 20 3a 20 61 73 63 69 69 54 6f 4d 6f 72 73 65 52 65 63 65 69 76 65 72 53 74 61 74 65 a 30 31 30 30
  //   31 31 31 30 30 6*78 2c 20 32 37 30 30 2c 20 32 37 33 66 2c 20 30 30 34 30 20 3a 20 6d 6f 72 73 65 52
  //   65 63 65 69 76 65 72 53 74 61 74 65 54 6f 41 73 63 69 69 a 30 31 30 30 31 31 31 30 31 6*78 2c 20 32
  //   37 34 30 2c 20 32 37 37 66 2c 20 30 30 34 30 20 3a 20 6d 6f 72 73 65 52 65 63 65 69 76 65 72 53 74
  //   61 74 65 54 6f 4e 6f 64 65 69 64 a 30 31 30 30 4*31 30 6*78 2c 20 32 37 38 30 2c 20 32 37 62 66 2c
  //   20 30 30 34 30 20 3a 20 6d 6f 72 73 65 52 65 63 65 69 76 65 72 53 74 61 74 65 54 6f 52 65 76 65 72
  //   73 65 64 4e 6f 64 65 69 64 a 30 31 30 31 30 10*78 2c 20 32 38 30 30 2c 20 32 62 66 66 2c 20 30 34 30
  //   30 20 3a 20 55 50 5f 44 4f 57 4e 5f 43 4f 55 4e 54 45 52 5f 52 4f 4d a 30 31 30 31 31 10*78 2c 20 32
  //   63 30 30 2c 20 32 66 66 66 2c 20 30 34 30 30 20 3a 20 6f 73 63 69 6c 6c 61 74 6f 72 73 a 30 31 31
  //   4*30 8*78 2c 20 33 30 30 30 2c 20 33 30 66 66 2c 20 30 31 30 30 20 3a 20 49 6e 74 54 6f 47 72 61 79
  //   a 30 31 31 30 30 30 31 8*78 2c 20 33 31 30 30 2c 20 33 31 66 66 2c 20 30 31 30 30 20 3a 20 47 72 61
  //   79 54 6f 49 6e 74 a 31 14*78 2c 20 34 30 30 30 2c 20 37 66 66 66 2c 20 34 30 30 30 20 3a 20 53 45 52
  //   49 41 4c 5f 54 52 41 4e 53 4d 49 54 54 45 52 5f 52 4f 4d a a a 44 65 74 61 69 6c 65 64 20 44 65 73
  //   63 72 69 70 74 69 6f 6e 3a a a 15*30 2c 20 4*30 2c 20 2d 30 30 31 2c 20 4*30 20 3a 20 54 61 62 6c 65
  //   20 4f 66 20 43 6f 6e 74 65 6e 74 73 a 30 31 30 30 30 10*78 2c 20 32 30 30 30 2c 20 32 33 66 66 2c 20
  //   30 34 30 30 20 3a 20 4d 4f 52 53 45 5f 52 45 43 45 49 56 45 52 5f 52 4f 4d a 20 20 41 6e 20 45 70 72
  //   6f 6d 20 53 74 61 74 65 20 4d 61 63 68 69 6e 65 20 74 68 61 74 20 72 65 63 65 69 76 65 73 20 73 65
  //   72 69 61 6c 20 6d 6f 72 73 65 20 63 6f 64 65 2e a 20 20 49 2f 4f 3a a 20 20 41 30 20 2e 2e 20 41 36
  //   2c 20 44 30 2e 2e 44 36 3a 20 73 74 61 74 65 20 28 36 20 73 74 61 74 65 20 62 69 74 73 20 28 36 34
  //   20 73 74 61 74 65 73 29 20 2b 20 31 20 70 61 72 69 74 79 20 62 69 74 29 a 20 20 41 37 3a 20 63 6c 6b
  //   20 28 73 65 72 69 61 6c 20 6d 6f 72 73 65 20 69 6e 70 75 74 29 a 20 20 41 38 3a 20 64 61 74 61 20 28
  //   64 65 6c 61 79 65 64 20 6d 6f 72 73 65 20 73 69 67 6e 61 6c 2c 20 73 61 6d 70 6c 65 64 20 61 74 20
  //   66 61 6c 6c 69 6e 67 20 65 64 67 65 20 6f 66 20 74 68 65 20 6d 6f 72 73 65 20 70 75 6c 73 65 2e 20
  //   30 20 66 6f 72 20 64 6f 74 2c 20 31 20 66 6f 72 20 64 61 73 68 29 a 20 20 41 39 3a 20 72 65 73 65 74
  //   20 28 73 65 74 73 20 74 68 65 20 73 74 61 74 65 20 30 29 a 20 20 44 37 3a 20 72 65 73 65 74 20 63 6f
  //   6d 70 6c 65 74 65 20 28 73 74 61 74 65 3d 3d 30 2c 20 72 65 61 64 79 20 74 6f 20 72 65 6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
endmodule

module EPROM_uart_receiver (
  input  rst,
  input  clk,
  input  serial_in,
  output [7:0] data_out,
  output data_ready,
  output framing_error,
  output parity_error
);

  wire clk0, clk1, d_ff_1_q, d_ff_3_q, next_char, not_1_out, not_2_out, OE_out, rst_state,
       skip_parity_bit_carry, start_clk;
  wire [7:0] counter_1_q, morseROM_data;

  not not_1 (not_1_out, start_clk);
  Counter #(.max('h7)) counter_1 (
    .load(not_1_out), .D(8'h2), .Q(counter_1_q), .clk(clk));  // open: count, carry, up, clr
  Counter #(.max('hc), .ongoal("stay")) skip_parity_bit (
    .carry(skip_parity_bit_carry), .clk(clk), .clr(start_clk));  // open: load, D, count, Q, up
  BitSelector bitselector_1 (.in(counter_1_q), .out(clk0), .sel(3'b010));
  D_Flip_Flop d_ff_1 (.clk(clk), .D(skip_parity_bit_carry), .Q(d_ff_1_q));  // open: Qn, preset, reset
  D_Flip_Flop d_ff_2 (.clk(clk), .D(clk0), .Q(clk1));  // open: Qn, preset, reset
  and and_1 (next_char, ~d_ff_1_q, skip_parity_bit_carry);  // AND_Gate
  ROM #(.addrWidth(15)) morseROM (
    .addr({4'b0111, serial_in, clk1, clk0, start_clk, data_out[6:0]}), .data(morseROM_data));
  Pull_Resistor pull_resistor_1 (.node({start_clk, data_out[6:0]}));
  or or_1 (rst_state, rst, next_char);
  not OE (OE_out, rst_state);
  assign {start_clk, data_out[6:0]} = OE_out ? morseROM_data : 8'bz;  // Controlled_Buffer controlled_buffer_1
  not not_2 (not_2_out, start_clk);
  D_Flip_Flop d_ff_3 (.clk(not_2_out), .D(1'b1), .Q(d_ff_3_q), .reset(next_char));  // open: Qn, preset
  D_Flip_Flop d_ff_4 (.clk(clk), .D(d_ff_3_q), .Q(data_ready), .reset(next_char));  // open: Qn, preset

  assign data_out[7] = 1'b0;

  // Notes on the sheet:
  //   contents of morseROM (hex, n*v repeats v):
  //   54 61 62 6c 65 20 4f 66 20 43 6f 6e 74 65 6e 74 73 3a a a 53 74 61 72 74 20 28 62 69 6e 29 6*20 28
  //   68 65 78 29 20 20 45 6e 64 20 20 53 69 7a 65 a 15*30 2c 20 4*30 2c 20 2d 30 30 31 2c 20 4*30 20 3a
  //   20 54 61 62 6c 65 20 4f 66 20 43 6f 6e 74 65 6e 74 73 a 30 31 30 30 30 10*78 2c 20 32 30 30 30 2c 20
  //   3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
endmodule
