// Logisim project morseROM_tests.circ as structural Verilog: 1 circuit, main circuit main
module main (
  input  [7:0] in_1,
  input  up_down,
  input  up_down2
);

  wire clock_1_out, clock_2_out, clock_3_out, clock_4_out, clock_5_out, clrscr, not_1_out, rst;
  wire [1:0] counter_2_q, xor_1_out;
  wire [7:0] asciiToMorseReceiverState_data, controlled_buffer_1_out, Documentation_data, grayToInt2_data,
       grayToInt3_data, grayToInt_data, intToGray_data, morseReceiverStateToAscii_data,
       morseReceiverStateToNodeId_data, oscillators_data, register_1_q, UP_DOWN_COINTER_ROM_data;
  wire [14:0] counter_1_q;

  Clock clock_1 (.out(clock_1_out));
  ROM #(.addrWidth(15)) Documentation (.addr(counter_1_q), .data(Documentation_data));
  Counter #(.max('hc8), .width(15)) counter_1 (
    .Q(counter_1_q), .carry(clrscr), .clk(clock_2_out));  // open: load, D, count, up, clr
  Clock clock_2 (.out(clock_2_out));
  Counter #(.max('h3), .width(2)) counter_2 (
    .Q(counter_2_q), .up(up_down), .clk(clock_1_out));  // open: load, D, count, carry, clr
  // Probe on counter_2_q
  POR por_1 (.out(rst));
  // Probe on xor_1_out
  xor xor_1 (xor_1_out[0], counter_2_q[0], counter_2_q[1]);
  buf buffer_1 (xor_1_out[1], counter_2_q[1]);
  ROM #(.addrWidth(15)) intToGray (.addr({7'b0110000, in_1}), .data(intToGray_data));
  ROM #(.addrWidth(15)) UP_DOWN_COINTER_ROM (
    .addr({5'b01010, xor_1_out, controlled_buffer_1_out}), .data(UP_DOWN_COINTER_ROM_data));
  ROM #(.addrWidth(15)) oscillators (.addr({5'b01011, up_down2, 1'b1, register_1_q}), .data(oscillators_data));
  // Probe on Documentation_data
  ROM #(.addrWidth(15)) asciiToMorseReceiverState (
    .addr({7'b0100110, Documentation_data}), .data(asciiToMorseReceiverState_data));
  Clock clock_3 (.out(clock_3_out));
  TTY #(.trigger("falling")) tty_1 (.data(Documentation_data[6:0]), .clk(clock_3_out), .clr(clrscr));  // open: we
  // Probe on intToGray_data
  ROM #(.addrWidth(15)) grayToInt (.addr({7'b0110001, intToGray_data}), .data(grayToInt_data));
  assign controlled_buffer_1_out = not_1_out ? UP_DOWN_COINTER_ROM_data : 8'bz;  // Controlled_Buffer controlled_buffer_1
  not not_1 (not_1_out, rst);
  Clock clock_4 (.out(clock_4_out));
  // Probe on controlled_buffer_1_out
  Pull_Resistor pull_resistor_1 (.node(controlled_buffer_1_out));
  // Probe on register_1_q
  Register register_1 (.D(oscillators_data), .Q(register_1_q), .clk(clock_4_out));  // open: en, clr
  // Probe on asciiToMorseReceiverState_data
  ROM #(.addrWidth(15)) grayToInt2 (.addr({7'b0110001, controlled_buffer_1_out}), .data(grayToInt2_data));
  ROM #(.addrWidth(15)) grayToInt3 (.addr({7'b0110001, register_1_q}), .data(grayToInt3_data));
  ROM #(.addrWidth(15)) morseReceiverStateToAscii (
    .addr({9'h9c, asciiToMorseReceiverState_data[5:0]}), .data(morseReceiverStateToAscii_data));
  ROM #(.addrWidth(15)) morseReceiverStateToNodeId (
    .addr({9'h9d, asciiToMorseReceiverState_data[5:0]}), .data(morseReceiverStateToNodeId_data));
  // Probe on grayToInt_data
  // Probe on grayToInt2_data
  // Probe on grayToInt3_data
  // Probe on morseReceiverStateToAscii_data
  Clock clock_5 (.out(clock_5_out));
  TTY #(.trigger("falling")) tty_2 (
    .data(morseReceiverStateToAscii_data[6:0]), .clk(clock_5_out), .clr(clrscr));  // open: we
  // Probe on morseReceiverStateToNodeId_data

  // Notes on the sheet:
  //   contents of Documentation (hex, n*v repeats v):
  //   54 61 62 6c 65 20 4f 66 20 43 6f 6e 74 65 6e 74 73 3a a a 53 74 61 72 74 20 28 62 69 6e 29 6*20 28
  //   68 65 78 29 20 20 45 6e 64 20 20 53 69 7a 65 a 15*30 2c 20 4*30 2c 20 2d 30 30 31 2c 20 4*30 20 3a
  //   20 54 61 62 6c 65 20 4f 66 20 43 6f 6e 74 65 6e 74 73 a 30 31 30 30 30 10*78 2c 20 32 30 30 30 2c 20
  //   32 33 66 66 2c 20 30 34 30 30 20 3a 20 4d 4f 52 53 45 5f 52 45 43 45 49 56 45 52 5f 52 4f 4d a 30 31
  //   30 30 31 30 30 8*78 2c 20 32 34 30 30 2c 20 32 34 66 66 2c 20 30 31 30 30 20 3a 20 4d 4f 52 53 45 5f
  //   54 52 41 4e 53 4d 49 54 54 45 52 5f 52 4f 4d a 30 31 30 30 31 30 31 8*78 2c 20 32 35 30 30 2c 20 32
  //   35 66 66 2c 20 30 31 30 30 20 3a 20 61 73 63 69 69 54 6f 4d 6f 72 73 65 54 72 61 6e 73 6d 69 74 74
  //   65 72 53 74 61 74 65 a 30 31 30 30 31 31 30 8*78 2c 20 32 36 30 30 2c 20 32 36 66 66 2c 20 30 31 30
  //   30 20 3a 20 61 73 63 69 69 54 6f 4d 6f 72 73 65 52 65 63 65 69 76 65 72 53 74 61 74 65 a 30 31 30 30
  //   31 31 31 30 30 6*78 2c 20 32 37 30 30 2c 20 32 37 33 66 2c 20 30 30 34 30 20 3a 20 6d 6f 72 73 65 52
  //   65 63 65 69 76 65 72 53 74 61 74 65 54 6f 41 73 63 69 69 a 30 31 30 30 31 31 31 30 31 6*78 2c 20 32
  //   37 34 30 2c 20 32 37 37 66 2c 20 30 30 34 30 20 3a 20 6d 6f 72 73 65 52 65 63 65 69 76 65 72 53 74
  //   61 74 65 54 6f 4e 6f 64 65 69 64 a 30 31 30 30 4*31 30 6*78 2c 20 32 37 38 30 2c 20 32 37 62 66 2c
  //   20 30 30 34 30 20 3a 20 6d 6f 72 73 65 52 65 63 65 69 76 65 72 53 74 61 74 65 54 6f 52 65 76 65 72
  //   73 65 64 4e 6f 64 65 69 64 a 30 31 30 31 30 10*78 2c 20 32 38 30 30 2c 20 32 62 66 66 2c 20 30 34 30
  //   30 20 3a 20 55 50 5f 44 4f 57 4e 5f 43 4f 55 4e 54 45 52 5f 52 4f 4d a 30 31 30 31 31 10*78 2c 20 32
  //   63 30 30 2c 20 32 66 66 66 2c 20 30 34 30 30 20 3a 20 6f 73 63 69 6c 6c 61 74 6f 72 73 a 30 31 31
  //   4*30 8*78 2c 20 33 30 30 30 2c 20 33 30 66 66 2c 20 30 31 30 30 20 3a 20 49 6e 74 54 6f 47 72 61 79
  //   a 30 31 31 30 30 30 31 8*78 2c 20 33 31 30 30 2c 20 33 31 66 66 2c 20 30 31 30 30 20 3a 20 47 72 61
  //   79 54 6f 49 6e 74 a 31 14*78 2c 20 34 30 30 30 2c 20 37 66 66 66 2c 20 34 30 30 30 20 3a 20 53 45 52
  //   49 41 4c 5f 54 52 41 4e 53 4d 49 54 54 45 52 5f 52 4f 4d a a a 44 65 74 61 69 6c 65 64 20 44 65 73
  //   63 72 69 70 74 69 6f 6e 3a a a 15*30 2c 20 4*30 2c 20 2d 30 30 31 2c 20 4*30 20 3a 20 54 61 62 6c 65
  //   20 4f 66 20 43 6f 6e 74 65 6e 74 73 a 30 31 30 30 30 10*78 2c 20 32 30 30 30 2c 20 32 33 66 66 2c 20
  //   30 34 30 30 20 3a 20 4d 4f 52 53 45 5f 52 45 43 45 49 56 45 52 5f 52 4f 4d a 20 20 41 6e 20 45 70 72
  //   6f 6d 20 53 74 61 74 65 20 4d 61 63 68 69 6e 65 20 74 68 61 74 20 72 65 63 65 69 76 65 73 20 73 65
  //   72 69 61 6c 20 6d 6f 72 73 65 20 63 6f 64 65 2e a 20 20 49 2f 4f 3a a 20 20 41 30 20 2e 2e 20 41 36
  //   2c 20 44 30 2e 2e 44 36 3a 20 73 74 61 74 65 20 28 36 20 73 74 61 74 65 20 62 69 74 73 20 28 36 34
  //   20 73 74 61 74 65 73 29 20 2b 20 31 20 70 61 72 69 74 79 20 62 69 74 29 a 20 20 41 37 3a 20 63 6c 6b
  //   20 28 73 65 72 69 61 6c 20 6d 6f 72 73 65 20 69 6e 70 75 74 29 a 20 20 41 38 3a 20 64 61 74 61 20 28
  //   64 65 6c 61 79 65 64 20 6d 6f 72 73 65 20 73 69 67 6e 61 6c 2c 20 73 61 6d 70 6c 65 64 20 61 74 20
  //   66 61 6c 6c 69 6e 67 20 65 64 67 65 20 6f 66 20 74 68 65 20 6d 6f 72 73 65 20 70 75 6c 73 65 2e 20
  //   30 20 66 6f 72 20 64 6f 74 2c 20 31 20 66 6f 72 20 64 61 73 68 29 a 20 20 41 39 3a 20 72 65 73 65 74
  //   20 28 73 65 74 73 20 74 68 65 20 73 74 61 74 65 20 30 29 a 20 20 44 37 3a 20 72 65 73 65 74 20 63 6f
  //   6d 70 6c 65 74 65 20 28 73 74 61 74 65 3d 3d 30 2c 20 72 65 61 64 79 20 74 6f 20 72 65 63 65 69 76
  //   65 20 74 68 65 20 6e 65 78 74 20 6d 6f 72 73 65 20 63 6f 64 65 29 a 20 20 a 30 31 30 30 31 30 30
  //   8*78 2c 20 32 34 30 30 2c 20 32 34 66 66 2c 20 30 31 30 30 20 3a 20 4d 4f 52 53 45 5f 54 52 41 4e 53
  //   4d 49 54 54 45 52 5f 52 4f 4d a 20 20 45 50 52 4f 4d 20 53 74 61 74 65 20 4d 61 63 68 69 6e 65 20 74
  //   68 61 74 20 67 65 6e 65 72 61 74 65 73 20 61 20 73 65 72 69 61 6c 20 4d 6f 72 73 65 20 6f 75 74 70
  //   75 74 20 66 6f 72 20 61 6e 20 69 6e 69 74 69 61 6c 20 69 6e 70 75 74 20 73 74 61 74 65 2a 2e a 20 20
  //   41 30 2e 2e 41 36 2c 44 30 2e 2e 44 36 3a 20 73 74 61 74 65 20 6f 66 20 74 68 65 20 73 74 61 74 65 2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
  //   contents of intToGray (hex, n*v repeats v):
  //   54 61 62 6c 65 20 4f 66 20 43 6f 6e 74 65 6e 74 73 3a a a 53 74 61 72 74 20 28 62 69 6e 29 6*20 28
  //   68 65 78 29 20 20 45 6e 64 20 20 53 69 7a 65 a 15*30 2c 20 4*30 2c 20 2d 30 30 31 2c 20 4*30 20 3a
  //   20 54 61 62 6c 65 20 4f 66 20 43 6f 6e 74 65 6e 74 73 a 30 31 30 30 30 10*78 2c 20 32 30 30 30 2c 20
  //   32 33 66 66 2c 20 30 34 30 30 20 3a 20 4d 4f 52 53 45 5f 52 45 43 45 49 56 45 52 5f 52 4f 4d a 30 31
  //   30 30 31 30 30 8*78 2c 20 32 34 30 30 2c 20 32 34 66 66 2c 20 30 31 30 30 20 3a 20 4d 4f 52 53 45 5f
  //   54 52 41 4e 53 4d 49 54 54 45 52 5f 52 4f 4d a 30 31 30 30 31 30 31 8*78 2c 20 32 35 30 30 2c 20 32
  //   35 66 66 2c 20 30 31 30 30 20 3a 20 61 73 63 69 69 54 6f 4d 6f 72 73 65 54 72 61 6e 73 6d 69 74 74
  //   65 72 53 74 61 74 65 a 30 31 30 30 31 31 30 8*78 2c 20 32 36 30 30 2c 20 32 36 66 66 2c 20 30 31 30
  //   30 20 3a 20 61 73 63 69 69 54 6f 4d 6f 72 73 65 52 65 63 65 69 76 65 72 53 74 61 74 65 a 30 31 30 30
  //   31 31 31 30 30 6*78 2c 20 32 37 30 30 2c 20 32 37 33 66 2c 20 30 30 34 30 20 3a 20 6d 6f 72 73 65 52
  //   65 63 65 69 76 65 72 53 74 61 74 65 54 6f 41 73 63 69 69 a 30 31 30 30 31 31 31 30 31 6*78 2c 20 32
  //   37 34 30 2c 20 32 37 37 66 2c 20 30 30 34 30 20 3a 20 6d 6f 72 73 65 52 65 63 65 69 76 65 72 53 74
  //   61 74 65 54 6f 4e 6f 64 65 69 64 a 30 31 30 30 4*31 30 6*78 2c 20 32 37 38 30 2c 20 32 37 62 66 2c
  //   20 30 30 34 30 20 3a 20 6d 6f 72 73 65 52 65 63 65 69 76 65 72 53 74 61 74 65 54 6f 52 65 76 65 72
  //   73 65 64 4e 6f 64 65 69 64 a 30 31 30 31 30 10*78 2c 20 32 38 30 30 2c 20 32 62 66 66 2c 20 30 34 30
  //   30 20 3a 20 55 50 5f 44 4f 57 4e 5f 43 4f 55 4e 54 45 52 5f 52 4f 4d a 30 31 30 31 31 10*78 2c 20 32
  //   63 30 30 2c 20 32 66 66 66 2c 20 30 34 30 30 20 3a 20 6f 73 63 69 6c 6c 61 74 6f 72 73 a 30 31 31
  //   4*30 8*78 2c 20 33 30 30 30 2c 20 33 30 66 66 2c 20 30 31 30 30 20 3a 20 49 6e 74 54 6f 47 72 61 79
  //   a 30 31 31 30 30 30 31 8*78 2c 20 33 31 30 30 2c 20 33 31 66 66 2c 20 30 31 30 30 20 3a 20 47 72 61
  //   79 54 6f 49 6e 74 a 31 14*78 2c 20 34 30 30 30 2c 20 37 66 66 66 2c 20 34 30 30 30 20 3a 20 53 45 52
  //   49 41 4c 5f 54 52 41 4e 53 4d 49 54 54 45 52 5f 52 4f 4d a a a 44 65 74 61 69 6c 65 64 20 44 65 73
  //   63 72 69 70 74 69 6f 6e 3a a a 15*30 2c 20 4*30 2c 20 2d 30 30 31 2c 20 4*30 20 3a 20 54 61 62 6c 65
  //   20 4f 66 20 43 6f 6e 74 65 6e 74 73 a 30 31 30 30 30 10*78 2c 20 32 30 30 30 2c 20 32 33 66 66 2c 20
  //   30 34 30 30 20 3a 20 4d 4f 52 53 45 5f 52 45 43 45 49 56 45 52 5f 52 4f 4d a 20 20 41 6e 20 45 70 72
  //   6f 6d 20 53 74 61 74 65 20 4d 61 63 68 69 6e 65 20 74 68 61 74 20 72 65 63 65 69 76 65 73 20 73 65
  //   72 69 61 6c 20 6d 6f 72 73 65 20 63 6f 64 65 2e a 20 20 49 2f 4f 3a a 20 20 41 30 20 2e 2e 20 41 36
  //   2c 20 44 30 2e 2e 44 36 3a 20 73 74 61 74 65 20 28 36 20 73 74 61 74 65 20 62 69 74 73 20 28 36 34
  //   20 73 74 61 74 65 73 29 20 2b 20 31 20 70 61 72 69 74 79 20 62 69 74 29 a 20 20 41 37 3a 20 63 6c 6b
  //   20 28 73 65 72 69 61 6c 20 6d 6f 72 73 65 20 69 6e 70 75 74 29 a 20 20 41 38 3a 20 64 61 74 61 20 28
  //   64 65 6c 61 79 65 64 20 6d 6f 72 73 65 20 73 69 67 6e 61 6c 2c 20 73 61 6d 70 6c 65 64 20 61 74 20
  //   66 61 6c 6c 69 6e 67 20 65 64 67 65 20 6f 66 20 74 68 65 20 6d 6f 72 73 65 20 70 75 6c 73 65 2e 20
  //   30 20 66 6f 72 20 64 6f 74 2c 20 31 20 66 6f 72 20 64 61 73 68 29 a 20 20 41 39 3a 20 72 65 73 65 74
  //   20 28 73 65 74 73 20 74 68 65 20 73 74 61 74 65 20 30 29 a 20 20 44 37 3a 20 72 65 73 65 74 20 63 6f
  //   6d 70 6c 65 74 65 20 28 73 74 61 74 65 3d 3d 30 2c 20 72 65 61 64 79 20 74 6f 20 72 65 63 65 69 76
  //   65 20 74 68 65 20 6e 65 78 74 20 6d 6f 72 73 65 20 63 6f 64 65 29 a 20 20 a 30 31 30 30 31 30 30
  //   8*78 2c 20 32 34 30 30 2c 20 32 34 66 66 2c 20 30 31 30 30 20 3a 20 4d 4f 52 53 45 5f 54 52 41 4e 53
  //   4d 49 54 54 45 52 5f 52 4f 4d a 20 20 45 50 52 4f 4d 20 53 74 61 74 65 20 4d 61 63 68 69 6e 65 20 74
  //   68 61 74 20 67 65 6e 65 72 61 74 65 73 20 61 20 73 65 72 69 61 6c 20 4d 6f 72 73 65 20 6f 75 74 70
  //   75 74 20 66 6f 72 20 61 6e 20 69 6e 69 74 69 61 6c 20 69 6e 70 75 74 20 73 74 61 74 65 2a 2e a 20 20
  //   41 30 2e 2e 41 36 2c 44 30 2e 2e 44 36 3a 20 73 74 61 74 65 20 6f 66 20 74 68 65 20 73 74 61 74 65 2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
  //   contents of UP_DOWN_COINTER_ROM (hex, n*v repeats v):
  //   54 61 62 6c 65 20 4f 66 20 43 6f 6e 74 65 6e 74 73 3a a a 53 74 61 72 74 20 28 62 69 6e 29 6*20 28
  //   68 65 78 29 20 20 45 6e 64 20 20 53 69 7a 65 a 15*30 2c 20 4*30 2c 20 2d 30 30 31 2c 20 4*30 20 3a
  //   20 54 61 62 6c 65 20 4f 66 20 43 6f 6e 74 65 6e 74 73 a 30 31 30 30 30 10*78 2c 20 32 30 30 30 2c 20
  //   32 33 66 66 2c 20 30 34 30 30 20 3a 20 4d 4f 52 53 45 5f 52 45 43 45 49 56 45 52 5f 52 4f 4d a 30 31
  //   30 30 31 30 30 8*78 2c 20 32 34 30 30 2c 20 32 34 66 66 2c 20 30 31 30 30 20 3a 20 4d 4f 52 53 45 5f
  //   54 52 41 4e 53 4d 49 54 54 45 52 5f 52 4f 4d a 30 31 30 30 31 30 31 8*78 2c 20 32 35 30 30 2c 20 32
  //   35 66 66 2c 20 30 31 30 30 20 3a 20 61 73 63 69 69 54 6f 4d 6f 72 73 65 54 72 61 6e 73 6d 69 74 74
  //   65 72 53 74 61 74 65 a 30 31 30 30 31 31 30 8*78 2c 20 32 36 30 30 2c 20 32 36 66 66 2c 20 30 31 30
  //   30 20 3a 20 61 73 63 69 69 54 6f 4d 6f 72 73 65 52 65 63 65 69 76 65 72 53 74 61 74 65 a 30 31 30 30
  //   31 31 31 30 30 6*78 2c 20 32 37 30 30 2c 20 32 37 33 66 2c 20 30 30 34 30 20 3a 20 6d 6f 72 73 65 52
  //   65 63 65 69 76 65 72 53 74 61 74 65 54 6f 41 73 63 69 69 a 30 31 30 30 31 31 31 30 31 6*78 2c 20 32
  //   37 34 30 2c 20 32 37 37 66 2c 20 30 30 34 30 20 3a 20 6d 6f 72 73 65 52 65 63 65 69 76 65 72 53 74
  //   61 74 65 54 6f 4e 6f 64 65 69 64 a 30 31 30 30 4*31 30 6*78 2c 20 32 37 38 30 2c 20 32 37 62 66 2c
  //   20 30 30 34 30 20 3a 20 6d 6f 72 73 65 52 65 63 65 69 76 65 72 53 74 61 74 65 54 6f 52 65 76 65 72
  //   73 65 64 4e 6f 64 65 69 64 a 30 31 30 31 30 10*78 2c 20 32 38 30 30 2c 20 32 62 66 66 2c 20 30 34 30
  //   30 20 3a 20 55 50 5f 44 4f 57 4e 5f 43 4f 55 4e 54 45 52 5f 52 4f 4d a 30 31 30 31 31 10*78 2c 20 32
  //   63 30 30 2c 20 32 66 66 66 2c 20 30 34 30 30 20 3a 20 6f 73 63 69 6c 6c 61 74 6f 72 73 a 30 31 31
  //   4*30 8*78 2c 20 33 30 30 30 2c 20 33 30 66 66 2c 20 30 31 30 30 20 3a 20 49 6e 74 54 6f 47 72 61 79
  //   a 30 31 31 30 30 30 31 8*78 2c 20 33 31 30 30 2c 20 33 31 66 66 2c 20 30 31 30 30 20 3a 20 47 72 61
  //   79 54 6f 49 6e 74 a 31 14*78 2c 20 34 30 30 30 2c 20 37 66 66 66 2c 20 34 30 30 30 20 3a 20 53 45 52
  //   49 41 4c 5f 54 52 41 4e 53 4d 49 54 54 45 52 5f 52 4f 4d a a a 44 65 74 61 69 6c 65 64 20 44 65 73
  //   63 72 69 70 74 69 6f 6e 3a a a 15*30 2c 20 4*30 2c 20 2d 30 30 31 2c 20 4*30 20 3a 20 54 61 62 6c 65
  //   20 4f 66 20 43 6f 6e 74 65 6e 74 73 a 30 31 30 30 30 10*78 2c 20 32 30 30 30 2c 20 32 33 66 66 2c 20
  //   30 34 30 30 20 3a 20 4d 4f 52 53 45 5f 52 45 43 45 49 56 45 52 5f 52 4f 4d a 20 20 41 6e 20 45 70 72
  //   6f 6d 20 53 74 61 74 65 20 4d 61 63 68 69 6e 65 20 74 68 61 74 20 72 65 63 65 69 76 65 73 20 73 65
  //   72 69 61 6c 20 6d 6f 72 73 65 20 63 6f 64 65 2e a 20 20 49 2f 4f 3a a 20 20 41 30 20 2e 2e 20 41 36
  //   2c 20 44 30 2e 2e 44 36 3a 20 73 74 61 74 65 20 28 36 20 73 74 61 74 65 20 62 69 74 73 20 28 36 34
  //   20 73 74 61 74 65 73 29 20 2b 20 31 20 70 61 72 69 74 79 20 62 69 74 29 a 20 20 41 37 3a 20 63 6c 6b
  //   20 28 73 65 72 69 61 6c 20 6d 6f 72 73 65 20 69 6e 70 75 74 29 a 20 20 41 38 3a 20 64 61 74 61 20 28
  //   64 65 6c 61 79 65 64 20 6d 6f 72 73 65 20 73 69 67 6e 61 6c 2c 20 73 61 6d 70 6c 65 64 20 61 74 20
  //   66 61 6c 6c 69 6e 67 20 65 64 67 65 20 6f 66 20 74 68 65 20 6d 6f 72 73 65 20 70 75 6c 73 65 2e 20
  //   30 20 66 6f 72 20 64 6f 74 2c 20 31 20 66 6f 72 20 64 61 73 68 29 a 20 20 41 39 3a 20 72 65 73 65 74
  //   20 28 73 65 74 73 20 74 68 65 20 73 74 61 74 65 20 30 29 a 20 20 44 37 3a 20 72 65 73 65 74 20 63 6f
  //   6d 70 6c 65 74 65 20 28 73 74 61 74 65 3d 3d 30 2c 20 72 65 61 64 79 20 74 6f 20 72 65 63 65 69 76
  //   65 20 74 68 65 20 6e 65 78 74 20 6d 6f 72 73 65 20 63 6f 64 65 29 a 20 20 a 30 31 30 30 31 30 30
  //   8*78 2c 20 32 34 30 30 2c 20 32 34 66 66 2c 20 30 31 30 30 20 3a 20 4d 4f 52 53 45 5f 54 52 41 4e 53
  //   4d 49 54 54 45 52 5f 52 4f 4d a 20 20 45 50 52 4f 4d 20 53 74 61 74 65 20 4d 61 63 68 69 6e 65 20 74
  //   68 61 74 20 67 65 6e 65 72 61 74 65 73 20 61 20 73 65 72 69 61 6c 20 4d 6f 72 73 65 20 6f 75 74 70
  //   75 74 20 66 6f 72 20 61 6e 20 69 6e 69 74 69 61 6c 20 69 6e 70 75 74 20 73 74 61 74 65 2a 2e a 20 20
  //   41 30 2e 2e 41 36 2c 44 30 2e 2e 44 36 3a 20 73 74 61 74 65 20 6f 66 20 74 68 65 20 73 74 61 74 65 2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
  //   contents of oscillators (hex, n*v repeats v):
  //   54 61 62 6c 65 20 4f 66 20 43 6f 6e 74 65 6e 74 73 3a a a 53 74 61 72 74 20 28 62 69 6e 29 6*20 28
  //   68 65 78 29 20 20 45 6e 64 20 20 53 69 7a 65 a 15*30 2c 20 4*30 2c 20 2d 30 30 31 2c 20 4*30 20 3a
  //   20 54 61 62 6c 65 20 4f 66 20 43 6f 6e 74 65 6e 74 73 a 30 31 30 30 30 10*78 2c 20 32 30 30 30 2c 20
  //   32 33 66 66 2c 20 30 34 30 30 20 3a 20 4d 4f 52 53 45 5f 52 45 43 45 49 56 45 52 5f 52 4f 4d a 30 31
  //   30 30 31 30 30 8*78 2c 20 32 34 30 30 2c 20 32 34 66 66 2c 20 30 31 30 30 20 3a 20 4d 4f 52 53 45 5f
  //   54 52 41 4e 53 4d 49 54 54 45 52 5f 52 4f 4d a 30 31 30 30 31 30 31 8*78 2c 20 32 35 30 30 2c 20 32
  //   35 66 66 2c 20 30 31 30 30 20 3a 20 61 73 63 69 69 54 6f 4d 6f 72 73 65 54 72 61 6e 73 6d 69 74 74
  //   65 72 53 74 61 74 65 a 30 31 30 30 31 31 30 8*78 2c 20 32 36 30 30 2c 20 32 36 66 66 2c 20 30 31 30
  //   30 20 3a 20 61 73 63 69 69 54 6f 4d 6f 72 73 65 52 65 63 65 69 76 65 72 53 74 61 74 65 a 30 31 30 30
  //   31 31 31 30 30 6*78 2c 20 32 37 30 30 2c 20 32 37 33 66 2c 20 30 30 34 30 20 3a 20 6d 6f 72 73 65 52
  //   65 63 65 69 76 65 72 53 74 61 74 65 54 6f 41 73 63 69 69 a 30 31 30 30 31 31 31 30 31 6*78 2c 20 32
  //   37 34 30 2c 20 32 37 37 66 2c 20 30 30 34 30 20 3a 20 6d 6f 72 73 65 52 65 63 65 69 76 65 72 53 74
  //   61 74 65 54 6f 4e 6f 64 65 69 64 a 30 31 30 30 4*31 30 6*78 2c 20 32 37 38 30 2c 20 32 37 62 66 2c
  //   20 30 30 34 30 20 3a 20 6d 6f 72 73 65 52 65 63 65 69 76 65 72 53 74 61 74 65 54 6f 52 65 76 65 72
  //   73 65 64 4e 6f 64 65 69 64 a 30 31 30 31 30 10*78 2c 20 32 38 30 30 2c 20 32 62 66 66 2c 20 30 34 30
  //   30 20 3a 20 55 50 5f 44 4f 57 4e 5f 43 4f 55 4e 54 45 52 5f 52 4f 4d a 30 31 30 31 31 10*78 2c 20 32
  //   63 30 30 2c 20 32 66 66 66 2c 20 30 34 30 30 20 3a 20 6f 73 63 69 6c 6c 61 74 6f 72 73 a 30 31 31
  //   4*30 8*78 2c 20 33 30 30 30 2c 20 33 30 66 66 2c 20 30 31 30 30 20 3a 20 49 6e 74 54 6f 47 72 61 79
  //   a 30 31 31 30 30 30 31 8*78 2c 20 33 31 30 30 2c 20 33 31 66 66 2c 20 30 31 30 30 20 3a 20 47 72 61
  //   79 54 6f 49 6e 74 a 31 14*78 2c 20 34 30 30 30 2c 20 37 66 66 66 2c 20 34 30 30 30 20 3a 20 53 45 52
  //   49 41 4c 5f 54 52 41 4e 53 4d 49 54 54 45 52 5f 52 4f 4d a a a 44 65 74 61 69 6c 65 64 20 44 65 73
  //   63 72 69 70 74 69 6f 6e 3a a a 15*30 2c 20 4*30 2c 20 2d 30 30 31 2c 20 4*30 20 3a 20 54 61 62 6c 65
  //   20 4f 66 20 43 6f 6e 74 65 6e 74 73 a 30 31 30 30 30 10*78 2c 20 32 30 30 30 2c 20 32 33 66 66 2c 20
  //   30 34 30 30 20 3a 20 4d 4f 52 53 45 5f 52 45 43 45 49 56 45 52 5f 52 4f 4d a 20 20 41 6e 20 45 70 72
  //   6f 6d 20 53 74 61 74 65 20 4d 61 63 68 69 6e 65 20 74 68 61 74 20 72 65 63 65 69 76 65 73 20 73 65
  //   72 69 61 6c 20 6d 6f 72 73 65 20 63 6f 64 65 2e a 20 20 49 2f 4f 3a a 20 20 41 30 20 2e 2e 20 41 36
  //   2c 20 44 30 2e 2e 44 36 3a 20 73 74 61 74 65 20 28 36 20 73 74 61 74 65 20 62 69 74 73 20 28 36 34
  //   20 73 74 61 74 65 73 29 20 2b 20 31 20 70 61 72 69 74 79 20 62 69 74 29 a 20 20 41 37 3a 20 63 6c 6b
  //   20 28 73 65 72 69 61 6c 20 6d 6f 72 73 65 20 69 6e 70 75 74 29 a 20 20 41 38 3a 20 64 61 74 61 20 28
  //   64 65 6c 61 79 65 64 20 6d 6f 72 73 65 20 73 69 67 6e 61 6c 2c 20 73 61 6d 70 6c 65 64 20 61 74 20
  //   66 61 6c 6c 69 6e 67 20 65 64 67 65 20 6f 66 20 74 68 65 20 6d 6f 72 73 65 20 70 75 6c 73 65 2e 20
  //   30 20 66 6f 72 20 64 6f 74 2c 20 31 20 66 6f 72 20 64 61 73 68 29 a 20 20 41 39 3a 20 72 65 73 65 74
  //   20 28 73 65 74 73 20 74 68 65 20 73 74 61 74 65 20 30 29 a 20 20 44 37 3a 20 72 65 73 65 74 20 63 6f
  //   6d 70 6c 65 74 65 20 28 73 74 61 74 65 3d 3d 30 2c 20 72 65 61 64 79 20 74 6f 20 72 65 63 65 69 76
  //   65 20 74 68 65 20 6e 65 78 74 20 6d 6f 72 73 65 20 63 6f 64 65 29 a 20 20 a 30 31 30 30 31 30 30
  //   8*78 2c 20 32 34 30 30 2c 20 32 34 66 66 2c 20 30 31 30 30 20 3a 20 4d 4f 52 53 45 5f 54 52 41 4e 53
  //   4d 49 54 54 45 52 5f 52 4f 4d a 20 20 45 50 52 4f 4d 20 53 74 61 74 65 20 4d 61 63 68 69 6e 65 20 74
  //   68 61 74 20 67 65 6e 65 72 61 74 65 73 20 61 20 73 65 72 69 61 6c 20 4d 6f 72 73 65 20 6f 75 74 70
  //   75 74 20 66 6f 72 20 61 6e 20 69 6e 69 74 69 61 6c 20 69 6e 70 75 74 20 73 74 61 74 65 2a 2e a 20 20
  //   41 30 2e 2e 41 36 2c 44 30 2e 2e 44 36 3a 20 73 74 61 74 65 20 6f 66 20 74 68 65 20 73 74 61 74 65 2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
  //   contents of asciiToMorseReceiverState (hex, n*v repeats v):
  //   54 61 62 6c 65 20 4f 66 20 43 6f 6e 74 65 6e 74 73 3a a a 53 74 61 72 74 20 28 62 69 6e 29 6*20 28
  //   68 65 78 29 20 20 45 6e 64 20 20 53 69 7a 65 a 15*30 2c 20 4*30 2c 20 2d 30 30 31 2c 20 4*30 20 3a
  //   20 54 61 62 6c 65 20 4f 66 20 43 6f 6e 74 65 6e 74 73 a 30 31 30 30 30 10*78 2c 20 32 30 30 30 2c 20
  //   3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
  //   contents of grayToInt (hex, n*v repeats v):
  //   54 61 62 6c 65 20 4f 66 20 43 6f 6e 74 65 6e 74 73 3a a a 53 74 61 72 74 20 28 62 69 6e 29 6*20 28
  //   68 65 78 29 20 20 45 6e 64 20 20 53 69 7a 65 a 15*30 2c 20 4*30 2c 20 2d 30 30 31 2c 20 4*30 20 3a
  //   20 54 61 62 6c 65 20 4f 66 20 43 6f 6e 74 65 6e 74 73 a 30 31 30 30 30 10*78 2c 20 32 30 30 30 2c 20
  //   3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
  //   contents of grayToInt2 (hex, n*v repeats v):
  //   54 61 62 6c 65 20 4f 66 20 43 6f 6e 74 65 6e 74 73 3a a a 53 74 61 72 74 20 28 62 69 6e 29 6*20 28
  //   68 65 78 29 20 20 45 6e 64 20 20 53 69 7a 65 a 15*30 2c 20 4*30 2c 20 2d 30 30 31 2c 20 4*30 20 3a
  //   20 54 61 62 6c 65 20 4f 66 20 43 6f 6e 74 65 6e 74 73 a 30 31 30 30 30 10*78 2c 20 32 30 30 30 2c 20
  //   3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
  //   contents of grayToInt3 (hex, n*v repeats v):
  //   54 61 62 6c 65 20 4f 66 20 43 6f 6e 74 65 6e 74 73 3a a a 53 74 61 72 74 20 28 62 69 6e 29 6*20 28
  //   68 65 78 29 20 20 45 6e 64 20 20 53 69 7a 65 a 15*30 2c 20 4*30 2c 20 2d 30 30 31 2c 20 4*30 20 3a
  //   20 54 61 62 6c 65 20 4f 66 20 43 6f 6e 74 65 6e 74 73 a 30 31 30 30 30 10*78 2c 20 32 30 30 30 2c 20
  //   3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
  //   contents of morseReceiverStateToAscii (hex, n*v repeats v):
  //   54 61 62 6c 65 20 4f 66 20 43 6f 6e 74 65 6e 74 73 3a a a 53 74 61 72 74 20 28 62 69 6e 29 6*20 28
  //   68 65 78 29 20 20 45 6e 64 20 20 53 69 7a 65 a 15*30 2c 20 4*30 2c 20 2d 30 30 31 2c 20 4*30 20 3a
  //   20 54 61 62 6c 65 20 4f 66 20 43 6f 6e 74 65 6e 74 73 a 30 31 30 30 30 10*78 2c 20 32 30 30 30 2c 20
  //   3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
  //   contents of morseReceiverStateToNodeId (hex, n*v repeats v):
  //   54 61 62 6c 65 20 4f 66 20 43 6f 6e 74 65 6e 74 73 3a a a 53 74 61 72 74 20 28 62 69 6e 29 6*20 28
  //   68 65 78 29 20 20 45 6e 64 20 20 53 69 7a 65 a 15*30 2c 20 4*30 2c 20 2d 30 30 31 2c 20 4*30 20 3a
  //   20 54 61 62 6c 65 20 4f 66 20 43 6f 6e 74 65 6e 74 73 a 30 31 30 30 30 10*78 2c 20 32 30 30 30 2c 20
  //   3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
endmodule
